// Logisim project cdm16_harward.circ as structural Verilog: 1 circuit, main circuit CDM16
module CDM16 (
  input  [15:0] adr,
  input  [15:0] val,
  input  in_3,
  input  [5:0] in_4,
  input  write,
  input  hold,
  output [15:0] id,
  output [15:0] x,
  output [15:0] y,
  output [15:0] command,
  output [15:0] collide
);

  wire and_2_out, and_3_out, and_4_out, and_5_out, and_6_out, and_7_out, and_8_out, cdm_16_1_p5, cdm_16_1_p6,
       cdm_16_1_p7, cl, code, comparator_1_eq, comparator_2_eq, comparator_3_eq, comparator_4_eq, d_ff_1_q,
       data, mem, not_1_out, not_2_out, not_3_out, not_4_out, not_5_out, or_1_out, pull_resistor_3_node,
       pull_resistor_5_node, pull_resistor_10_node, pull_resistor_11_node, read_write, transistor_2_out,
       word, write_t;
  wire [15:0] cdm_16_1_p11, cdm_16_1_p12, cdm_16_1_p13, controlled_buffer_2_out, rom_1_p4, transistor_3_out;

  // Debugger debugger_1: pin names not known
  and and_1 (write_t, write, d_ff_1_q);
  // Probe on in_4
  D_Flip_Flop d_ff_1 (.clk(not_1_out), .D(or_1_out), .Q(d_ff_1_q));  // open: Qn, preset, en, reset
  not not_1 (not_1_out, cl);
  or or_1 (or_1_out, write, hold);
  // CdM_16 cdm_16_1: pin names not known; wires that end beside it: in_3, in_4, d_ff_1_q, cl, cdm_16_1_p5, cdm_16_1_p6, cdm_16_1_p7, mem, read_write, word, cdm_16_1_p11, cdm_16_1_p12, cdm_16_1_p13
  // Probe on cdm_16_1_p6
  Clock clock_1 (.out(cl));
  // Probe on cdm_16_1_p5
  not not_2 (not_2_out, write_t);
  not not_3 (not_3_out, write_t);
  assign cdm_16_1_p13 = and_3_out ? controlled_buffer_2_out : 16'bz;  // Controlled_Buffer controlled_buffer_1
  assign controlled_buffer_2_out = and_2_out ? cdm_16_1_p12 : 16'bz;  // Controlled_Buffer controlled_buffer_2
  and and_2 (and_2_out, not_2_out, not_4_out);
  not not_4 (not_4_out, read_write);
  not not_5 (not_5_out, read_write);
  and and_3 (and_3_out, not_3_out, read_write);
  Pull_Resistor pull_resistor_1 (.node(code));
  Pull_Resistor #(.pull(1)) pull_resistor_2 (.node(data));
  Pull_Resistor pull_resistor_3 (.node(pull_resistor_3_node));
  Transistor #(.gate("br")) transistor_1 (.in(pull_resistor_3_node), .out(data), .gate(write_t));
  Decoder decoder_1 (.out0(code), .out1(pull_resistor_3_node), .sel(cdm_16_1_p7), .en(mem));
  Transistor transistor_2 (.in(not_5_out), .out(transistor_2_out), .gate(write_t));
  Pull_Resistor #(.pull(1)) pull_resistor_4 (.node(transistor_2_out));
  Transistor #(.\type ("n"), .width(16)) transistor_3 (.in(adr), .out(transistor_3_out), .gate(write_t));
  Transistor #(.gate("br"), .width(16)) transistor_4 (.in(cdm_16_1_p11), .out(transistor_3_out), .gate(write_t));
  // Probe on transistor_3_out
  Pull_Resistor pull_resistor_5 (.node(pull_resistor_5_node));
  Transistor transistor_5 (.in(word), .out(pull_resistor_5_node), .gate(write_t));
  Comparator #(.width(16)) comparator_1 (.a(transistor_3_out), .b(16'h80), .eq(comparator_1_eq));  // open: gt, lt
  Pull_Resistor pull_resistor_6 (.node(comparator_1_eq));
  Comparator #(.width(16)) comparator_2 (.a(transistor_3_out), .b(16'h82), .eq(comparator_2_eq));  // open: gt, lt
  Pull_Resistor pull_resistor_7 (.node(comparator_2_eq));
  Comparator #(.width(16)) comparator_3 (.a(transistor_3_out), .b(16'h84), .eq(comparator_3_eq));  // open: gt, lt
  Pull_Resistor pull_resistor_8 (.node(comparator_3_eq));
  Comparator #(.width(16)) comparator_4 (.a(transistor_3_out), .b(16'h86), .eq(comparator_4_eq));  // open: gt, lt
  Pull_Resistor pull_resistor_9 (.node(comparator_4_eq));
  Pull_Resistor pull_resistor_10 (.node(pull_resistor_10_node));
  Comparator #(.width(16)) comparator_5 (.a(transistor_3_out), .b(16'h88), .eq(pull_resistor_10_node));  // open: gt, lt
  Pull_Resistor pull_resistor_11 (.node(pull_resistor_11_node));
  Transistor #(.gate("br")) transistor_6 (.in(read_write), .out(pull_resistor_11_node), .gate(write_t));
  // ROM rom_1: pin names not known; wires that end beside it: transistor_3_out, code, word, rom_1_p4
  // RAM ram_1: pin names not known; wires that end beside it: transistor_3_out, pull_resistor_5_node, data, cl, pull_resistor_11_node, controlled_buffer_2_out
  Register #(.width(16)) register_1 (.D(controlled_buffer_2_out), .Q(id), .clk(and_4_out));  // open: en, clr
  and and_4 (and_4_out, comparator_1_eq, data, transistor_2_out);
  Register #(.width(16)) register_2 (.D(controlled_buffer_2_out), .Q(x), .clk(and_5_out));  // open: en, clr
  and and_5 (and_5_out, comparator_2_eq, data, transistor_2_out);
  Register #(.width(16)) register_3 (.D(controlled_buffer_2_out), .Q(y), .clk(and_6_out));  // open: en, clr
  and and_6 (and_6_out, comparator_3_eq, data, transistor_2_out);
  Register #(.width(16)) register_4 (.D(controlled_buffer_2_out), .Q(command), .clk(and_7_out));  // open: en, clr
  and and_7 (and_7_out, comparator_4_eq, data, transistor_2_out);
  Register #(.width(16)) register_5 (.D(controlled_buffer_2_out), .Q(collide), .clk(and_8_out));  // open: en, clr
  and and_8 (and_8_out, pull_resistor_10_node, data, transistor_2_out);
  Transistor #(.width(16)) transistor_7 (.in(rom_1_p4), .out(controlled_buffer_2_out), .gate(write_t));
  Transistor #(.\type ("n"), .width(16)) transistor_8 (.in(val), .out(controlled_buffer_2_out), .gate(write_t));

  // Notes on the sheet:
  //   hold приостанавливает процессор
  //   write как hold но даёт возможность писать в ОЗУ
endmodule
