// Logisim project main.circ as structural Verilog: 34 circuits, main circuit main
module main (
);

  wire button, button_2_out, button_3_out, cdm16_1_collide, cdm16_1_drawing, clk, collide,
       collide_check_enemy, collide_check_player, collide_check_wall, command_draw, drawer_1_out_7,
       drawer_1_out_10, drawer_2_out_6, drawer_2_out_7, drawer_2_out_10, drawer_3_out_6, drawer_3_out_7,
       drawer_3_out_10, drawing, end_cycle, hold, hold_1, lose, main_thread_1_request, main_thread_1_write,
       player_thread_1_request, priority_thread_selector_1_access, priority_thread_selector_1_access_2,
       priority_thread_selector_1_writing, processor_drawing, run, shot, wait_int, win, write_sync;
  wire [2:0] multiplexer_1_out, multiplexer_2_out, x_vec;
  wire [3:0] bit_extender_1_out, bit_extender_2_out, bit_extender_3_out;
  wire [4:0] bullet_thread_1_x, bullet_thread_1_y, drawer_1_out_9, drawer_2_out_9, drawer_3_out_9,
       main_thread_1_x_2, main_thread_1_y_2, player_thread_1_x, player_thread_1_y;
  wire [15:0] bullet_thread_1_command, bullet_thread_1_id, cdm16_1_command, cdm16_1_id, cdm16_1_x, cdm16_1_y,
       divider_1_out, divider_1_rem, divider_2_rem, hp, main_thread_1_adr, main_thread_1_command_2,
       main_thread_1_id_2, main_thread_1_val, player_thread_1_command, player_thread_1_id, score, x_col,
       y_col;
  wire [31:0] drawer_1_out_8, drawer_2_out_8, drawer_3_out_8, multilayer_video_buffer_32x32_1_out_37,
       multilayer_video_buffer_32x32_1_out_38, multilayer_video_buffer_32x32_1_out_39,
       multilayer_video_buffer_32x32_1_out_40, multilayer_video_buffer_32x32_1_out_41,
       multilayer_video_buffer_32x32_1_out_42, multilayer_video_buffer_32x32_1_out_43,
       multilayer_video_buffer_32x32_1_out_44, multilayer_video_buffer_32x32_1_out_45,
       multilayer_video_buffer_32x32_1_out_46, multilayer_video_buffer_32x32_1_out_47,
       multilayer_video_buffer_32x32_1_out_48, multilayer_video_buffer_32x32_1_out_49,
       multilayer_video_buffer_32x32_1_out_50, multilayer_video_buffer_32x32_1_out_51,
       multilayer_video_buffer_32x32_1_out_52, multilayer_video_buffer_32x32_1_out_53,
       multilayer_video_buffer_32x32_1_out_54, multilayer_video_buffer_32x32_1_out_55,
       multilayer_video_buffer_32x32_1_out_56, multilayer_video_buffer_32x32_1_out_57,
       multilayer_video_buffer_32x32_1_out_58, multilayer_video_buffer_32x32_1_out_59,
       multilayer_video_buffer_32x32_1_out_60, multilayer_video_buffer_32x32_1_out_61,
       multilayer_video_buffer_32x32_1_out_62, multilayer_video_buffer_32x32_1_out_63,
       multilayer_video_buffer_32x32_1_out_64, multilayer_video_buffer_32x32_1_out_65,
       multilayer_video_buffer_32x32_1_out_66, multilayer_video_buffer_32x32_1_out_67,
       multilayer_video_buffer_32x32_1_out_68, multilayer_video_buffer_32x32_2_out_37,
       multilayer_video_buffer_32x32_2_out_38, multilayer_video_buffer_32x32_2_out_39,
       multilayer_video_buffer_32x32_2_out_40, multilayer_video_buffer_32x32_2_out_41,
       multilayer_video_buffer_32x32_2_out_42, multilayer_video_buffer_32x32_2_out_43,
       multilayer_video_buffer_32x32_2_out_44, multilayer_video_buffer_32x32_2_out_45,
       multilayer_video_buffer_32x32_2_out_46, multilayer_video_buffer_32x32_2_out_47,
       multilayer_video_buffer_32x32_2_out_48, multilayer_video_buffer_32x32_2_out_49,
       multilayer_video_buffer_32x32_2_out_50, multilayer_video_buffer_32x32_2_out_51,
       multilayer_video_buffer_32x32_2_out_52, multilayer_video_buffer_32x32_2_out_53,
       multilayer_video_buffer_32x32_2_out_54, multilayer_video_buffer_32x32_2_out_55,
       multilayer_video_buffer_32x32_2_out_56, multilayer_video_buffer_32x32_2_out_57,
       multilayer_video_buffer_32x32_2_out_58, multilayer_video_buffer_32x32_2_out_59,
       multilayer_video_buffer_32x32_2_out_60, multilayer_video_buffer_32x32_2_out_61,
       multilayer_video_buffer_32x32_2_out_62, multilayer_video_buffer_32x32_2_out_63,
       multilayer_video_buffer_32x32_2_out_64, multilayer_video_buffer_32x32_2_out_65,
       multilayer_video_buffer_32x32_2_out_66, multilayer_video_buffer_32x32_2_out_67,
       multilayer_video_buffer_32x32_2_out_68, video_buffer_32x32_1_out_5, video_buffer_32x32_1_out_6,
       video_buffer_32x32_1_out_7, video_buffer_32x32_1_out_8, video_buffer_32x32_1_out_9,
       video_buffer_32x32_1_out_10, video_buffer_32x32_1_out_11, video_buffer_32x32_1_out_12,
       video_buffer_32x32_1_out_13, video_buffer_32x32_1_out_14, video_buffer_32x32_1_out_15,
       video_buffer_32x32_1_out_16, video_buffer_32x32_1_out_17, video_buffer_32x32_1_out_18,
       video_buffer_32x32_1_out_19, video_buffer_32x32_1_out_20, video_buffer_32x32_1_out_21,
       video_buffer_32x32_1_out_22, video_buffer_32x32_1_out_23, video_buffer_32x32_1_out_24,
       video_buffer_32x32_1_out_25, video_buffer_32x32_1_out_26, video_buffer_32x32_1_out_27,
       video_buffer_32x32_1_out_28, video_buffer_32x32_1_out_29, video_buffer_32x32_1_out_30,
       video_buffer_32x32_1_out_31, video_buffer_32x32_1_out_32, video_buffer_32x32_1_out_33,
       video_buffer_32x32_1_out_34, video_buffer_32x32_1_out_35, video_buffer_32x32_1_out_36;

  Clock clock_1 (.out(clk));
  or or_1 (end_cycle, win, lose);
  main_thread main_thread_1 (
    .ID_2(main_thread_1_id_2), .X_2(main_thread_1_x_2), .Y_2(main_thread_1_y_2),
    .Command_2(main_thread_1_command_2), .clock(clk), .drawing(drawing), .write(main_thread_1_write),
    .val(main_thread_1_val), .adr(main_thread_1_adr), .x_col(x_col), .y_col(y_col), .id(cdm16_1_id),
    .x(cdm16_1_x), .y(cdm16_1_y), .command(cdm16_1_command), .end_cycle(end_cycle),
    .processor_drawing(processor_drawing), .run(run), .wait_int(wait_int),
    .collide_check_enemy(collide_check_enemy), .collide_check_wall(collide_check_wall), .collide(collide),
    .win(win), .lose(lose), .hold(hold_1), .request(main_thread_1_request),
    .response(priority_thread_selector_1_access), .write_sync(write_sync), .draw(command_draw));
  CDM16 cdm16_1 (
    .adr(main_thread_1_adr), .val(main_thread_1_val), .id(cdm16_1_id), .x(cdm16_1_x), .y(cdm16_1_y),
    .command(cdm16_1_command), .collide(cdm16_1_collide), .write(main_thread_1_write), .hold(hold),
    .clock(clk), .wait_int__checker(wait_int), .run(run), .drawing(cdm16_1_drawing), .score(score),
    .gg(lose), .win(win), .hp(hp), .end_cycle(end_cycle), .holded(write_sync));  // open: button
  Pull_Resistor pull_resistor_1 (.node(main_thread_1_write));
  drawer drawer_1 (
    .out_6(drawing), .out_8(drawer_1_out_8), .out_9(drawer_1_out_9), .out_10(drawer_1_out_10),
    .in_1(main_thread_1_id_2), .in_2(main_thread_1_x_2), .in_3(main_thread_1_y_2),
    .in_4(main_thread_1_command_2), .out_7(drawer_1_out_7), .clk(clk));
  video_buffer_32x32 video_buffer_32x32_1 (
    .out_5(video_buffer_32x32_1_out_5), .out_6(video_buffer_32x32_1_out_6),
    .out_7(video_buffer_32x32_1_out_7), .out_8(video_buffer_32x32_1_out_8),
    .out_9(video_buffer_32x32_1_out_9), .out_10(video_buffer_32x32_1_out_10),
    .out_11(video_buffer_32x32_1_out_11), .out_12(video_buffer_32x32_1_out_12),
    .out_13(video_buffer_32x32_1_out_13), .out_14(video_buffer_32x32_1_out_14),
    .out_15(video_buffer_32x32_1_out_15), .out_16(video_buffer_32x32_1_out_16),
    .out_17(video_buffer_32x32_1_out_17), .out_18(video_buffer_32x32_1_out_18),
    .out_19(video_buffer_32x32_1_out_19), .out_20(video_buffer_32x32_1_out_20),
    .out_21(video_buffer_32x32_1_out_21), .out_22(video_buffer_32x32_1_out_22),
    .out_23(video_buffer_32x32_1_out_23), .out_24(video_buffer_32x32_1_out_24),
    .out_25(video_buffer_32x32_1_out_25), .out_26(video_buffer_32x32_1_out_26),
    .out_27(video_buffer_32x32_1_out_27), .out_28(video_buffer_32x32_1_out_28),
    .out_29(video_buffer_32x32_1_out_29), .out_30(video_buffer_32x32_1_out_30),
    .out_31(video_buffer_32x32_1_out_31), .out_32(video_buffer_32x32_1_out_32),
    .out_33(video_buffer_32x32_1_out_33), .out_34(video_buffer_32x32_1_out_34),
    .out_35(video_buffer_32x32_1_out_35), .out_36(video_buffer_32x32_1_out_36), .write(drawer_1_out_7),
    .\input (drawer_1_out_8), .y(drawer_1_out_9), .show(drawer_1_out_10));
  multilayer_video_buffer_32x32 multilayer_video_buffer_32x32_1 (
    .in_1(video_buffer_32x32_1_out_5), .in_2(video_buffer_32x32_1_out_6), .in_3(video_buffer_32x32_1_out_7),
    .in_4(video_buffer_32x32_1_out_8), .in_5(video_buffer_32x32_1_out_9), .in_6(video_buffer_32x32_1_out_10),
    .in_8(video_buffer_32x32_1_out_11), .in_12(video_buffer_32x32_1_out_12),
    .in_13(video_buffer_32x32_1_out_13), .in_14(video_buffer_32x32_1_out_14),
    .in_15(video_buffer_32x32_1_out_15), .in_16(video_buffer_32x32_1_out_16),
    .in_17(video_buffer_32x32_1_out_17), .in_18(video_buffer_32x32_1_out_18),
    .in_19(video_buffer_32x32_1_out_19), .in_20(video_buffer_32x32_1_out_20),
    .in_21(video_buffer_32x32_1_out_21), .in_22(video_buffer_32x32_1_out_22),
    .in_23(video_buffer_32x32_1_out_23), .in_24(video_buffer_32x32_1_out_24),
    .in_25(video_buffer_32x32_1_out_25), .in_26(video_buffer_32x32_1_out_26),
    .in_27(video_buffer_32x32_1_out_27), .in_28(video_buffer_32x32_1_out_28),
    .in_29(video_buffer_32x32_1_out_29), .in_30(video_buffer_32x32_1_out_30),
    .in_31(video_buffer_32x32_1_out_31), .in_32(video_buffer_32x32_1_out_32),
    .in_33(video_buffer_32x32_1_out_33), .in_34(video_buffer_32x32_1_out_34),
    .in_35(video_buffer_32x32_1_out_35), .in_36(video_buffer_32x32_1_out_36),
    .out_37(multilayer_video_buffer_32x32_1_out_37), .out_38(multilayer_video_buffer_32x32_1_out_38),
    .out_39(multilayer_video_buffer_32x32_1_out_39), .out_40(multilayer_video_buffer_32x32_1_out_40),
    .out_41(multilayer_video_buffer_32x32_1_out_41), .out_42(multilayer_video_buffer_32x32_1_out_42),
    .out_43(multilayer_video_buffer_32x32_1_out_43), .out_44(multilayer_video_buffer_32x32_1_out_44),
    .out_45(multilayer_video_buffer_32x32_1_out_45), .out_46(multilayer_video_buffer_32x32_1_out_46),
    .out_47(multilayer_video_buffer_32x32_1_out_47), .out_48(multilayer_video_buffer_32x32_1_out_48),
    .out_49(multilayer_video_buffer_32x32_1_out_49), .out_50(multilayer_video_buffer_32x32_1_out_50),
    .out_51(multilayer_video_buffer_32x32_1_out_51), .out_52(multilayer_video_buffer_32x32_1_out_52),
    .out_53(multilayer_video_buffer_32x32_1_out_53), .out_54(multilayer_video_buffer_32x32_1_out_54),
    .out_55(multilayer_video_buffer_32x32_1_out_55), .out_56(multilayer_video_buffer_32x32_1_out_56),
    .out_57(multilayer_video_buffer_32x32_1_out_57), .out_58(multilayer_video_buffer_32x32_1_out_58),
    .out_59(multilayer_video_buffer_32x32_1_out_59), .out_60(multilayer_video_buffer_32x32_1_out_60),
    .out_61(multilayer_video_buffer_32x32_1_out_61), .out_62(multilayer_video_buffer_32x32_1_out_62),
    .out_63(multilayer_video_buffer_32x32_1_out_63), .out_64(multilayer_video_buffer_32x32_1_out_64),
    .out_65(multilayer_video_buffer_32x32_1_out_65), .out_66(multilayer_video_buffer_32x32_1_out_66),
    .out_67(multilayer_video_buffer_32x32_1_out_67), .out_68(multilayer_video_buffer_32x32_1_out_68),
    .write(drawer_2_out_7), .\input (drawer_2_out_8), .y(drawer_2_out_9), .show(drawer_2_out_10));
  priority_thread_selector priority_thread_selector_1 (
    .access(priority_thread_selector_1_access), .request(main_thread_1_request),
    .access_2(priority_thread_selector_1_access_2), .request_2(player_thread_1_request),
    .writing(priority_thread_selector_1_writing));  // open: access_3, request_3
  or or_2 (hold, priority_thread_selector_1_writing, hold_1);
  and and_1 (processor_drawing, cdm16_1_drawing, drawing);
  multilayer_video_buffer_32x32 multilayer_video_buffer_32x32_2 (
    .in_1(multilayer_video_buffer_32x32_1_out_37), .in_2(multilayer_video_buffer_32x32_1_out_38),
    .in_3(multilayer_video_buffer_32x32_1_out_39), .in_4(multilayer_video_buffer_32x32_1_out_40),
    .in_5(multilayer_video_buffer_32x32_1_out_41), .in_6(multilayer_video_buffer_32x32_1_out_42),
    .in_8(multilayer_video_buffer_32x32_1_out_43), .in_12(multilayer_video_buffer_32x32_1_out_44),
    .in_13(multilayer_video_buffer_32x32_1_out_45), .in_14(multilayer_video_buffer_32x32_1_out_46),
    .in_15(multilayer_video_buffer_32x32_1_out_47), .in_16(multilayer_video_buffer_32x32_1_out_48),
    .in_17(multilayer_video_buffer_32x32_1_out_49), .in_18(multilayer_video_buffer_32x32_1_out_50),
    .in_19(multilayer_video_buffer_32x32_1_out_51), .in_20(multilayer_video_buffer_32x32_1_out_52),
    .in_21(multilayer_video_buffer_32x32_1_out_53), .in_22(multilayer_video_buffer_32x32_1_out_54),
    .in_23(multilayer_video_buffer_32x32_1_out_55), .in_24(multilayer_video_buffer_32x32_1_out_56),
    .in_25(multilayer_video_buffer_32x32_1_out_57), .in_26(multilayer_video_buffer_32x32_1_out_58),
    .in_27(multilayer_video_buffer_32x32_1_out_59), .in_28(multilayer_video_buffer_32x32_1_out_60),
    .in_29(multilayer_video_buffer_32x32_1_out_61), .in_30(multilayer_video_buffer_32x32_1_out_62),
    .in_31(multilayer_video_buffer_32x32_1_out_63), .in_32(multilayer_video_buffer_32x32_1_out_64),
    .in_33(multilayer_video_buffer_32x32_1_out_65), .in_34(multilayer_video_buffer_32x32_1_out_66),
    .in_35(multilayer_video_buffer_32x32_1_out_67), .in_36(multilayer_video_buffer_32x32_1_out_68),
    .out_37(multilayer_video_buffer_32x32_2_out_37), .out_38(multilayer_video_buffer_32x32_2_out_38),
    .out_39(multilayer_video_buffer_32x32_2_out_39), .out_40(multilayer_video_buffer_32x32_2_out_40),
    .out_41(multilayer_video_buffer_32x32_2_out_41), .out_42(multilayer_video_buffer_32x32_2_out_42),
    .out_43(multilayer_video_buffer_32x32_2_out_43), .out_44(multilayer_video_buffer_32x32_2_out_44),
    .out_45(multilayer_video_buffer_32x32_2_out_45), .out_46(multilayer_video_buffer_32x32_2_out_46),
    .out_47(multilayer_video_buffer_32x32_2_out_47), .out_48(multilayer_video_buffer_32x32_2_out_48),
    .out_49(multilayer_video_buffer_32x32_2_out_49), .out_50(multilayer_video_buffer_32x32_2_out_50),
    .out_51(multilayer_video_buffer_32x32_2_out_51), .out_52(multilayer_video_buffer_32x32_2_out_52),
    .out_53(multilayer_video_buffer_32x32_2_out_53), .out_54(multilayer_video_buffer_32x32_2_out_54),
    .out_55(multilayer_video_buffer_32x32_2_out_55), .out_56(multilayer_video_buffer_32x32_2_out_56),
    .out_57(multilayer_video_buffer_32x32_2_out_57), .out_58(multilayer_video_buffer_32x32_2_out_58),
    .out_59(multilayer_video_buffer_32x32_2_out_59), .out_60(multilayer_video_buffer_32x32_2_out_60),
    .out_61(multilayer_video_buffer_32x32_2_out_61), .out_62(multilayer_video_buffer_32x32_2_out_62),
    .out_63(multilayer_video_buffer_32x32_2_out_63), .out_64(multilayer_video_buffer_32x32_2_out_64),
    .out_65(multilayer_video_buffer_32x32_2_out_65), .out_66(multilayer_video_buffer_32x32_2_out_66),
    .out_67(multilayer_video_buffer_32x32_2_out_67), .out_68(multilayer_video_buffer_32x32_2_out_68),
    .write(drawer_3_out_7), .\input (drawer_3_out_8), .y(drawer_3_out_9), .show(drawer_3_out_10));
  DotMatrix #(.inputtype("row"), .matrixcols(32), .matrixrows(32)) dotmatrix_1 (
    .row0(multilayer_video_buffer_32x32_2_out_37), .row1(multilayer_video_buffer_32x32_2_out_38),
    .row2(multilayer_video_buffer_32x32_2_out_39), .row3(multilayer_video_buffer_32x32_2_out_40),
    .row4(multilayer_video_buffer_32x32_2_out_41), .row5(multilayer_video_buffer_32x32_2_out_42),
    .row6(multilayer_video_buffer_32x32_2_out_43), .row7(multilayer_video_buffer_32x32_2_out_44),
    .row8(multilayer_video_buffer_32x32_2_out_45), .row9(multilayer_video_buffer_32x32_2_out_46),
    .row10(multilayer_video_buffer_32x32_2_out_47), .row11(multilayer_video_buffer_32x32_2_out_48),
    .row12(multilayer_video_buffer_32x32_2_out_49), .row13(multilayer_video_buffer_32x32_2_out_50),
    .row14(multilayer_video_buffer_32x32_2_out_51), .row15(multilayer_video_buffer_32x32_2_out_52),
    .row16(multilayer_video_buffer_32x32_2_out_53), .row17(multilayer_video_buffer_32x32_2_out_54),
    .row18(multilayer_video_buffer_32x32_2_out_55), .row19(multilayer_video_buffer_32x32_2_out_56),
    .row20(multilayer_video_buffer_32x32_2_out_57), .row21(multilayer_video_buffer_32x32_2_out_58),
    .row22(multilayer_video_buffer_32x32_2_out_59), .row23(multilayer_video_buffer_32x32_2_out_60),
    .row24(multilayer_video_buffer_32x32_2_out_61), .row25(multilayer_video_buffer_32x32_2_out_62),
    .row26(multilayer_video_buffer_32x32_2_out_63), .row27(multilayer_video_buffer_32x32_2_out_64),
    .row28(multilayer_video_buffer_32x32_2_out_65), .row29(multilayer_video_buffer_32x32_2_out_66),
    .row30(multilayer_video_buffer_32x32_2_out_67), .row31(multilayer_video_buffer_32x32_2_out_68));
  drawer drawer_2 (
    .out_6(drawer_2_out_6), .out_8(drawer_2_out_8), .out_9(drawer_2_out_9), .out_10(drawer_2_out_10),
    .in_1(player_thread_1_id), .in_2(player_thread_1_x), .in_3(player_thread_1_y),
    .in_4(player_thread_1_command), .out_7(drawer_2_out_7), .clk(clk));
  player_thread player_thread_1 (
    .px(x_vec), .run(run), .end_cycle(end_cycle), .collide_check_player(collide_check_player),
    .id(player_thread_1_id), .x(player_thread_1_x), .y(player_thread_1_y), .command(player_thread_1_command),
    .clk(clk), .drawing(drawer_2_out_6), .shot(shot), .button(button), .write(main_thread_1_write),
    .val(main_thread_1_val), .adr(main_thread_1_adr), .response(priority_thread_selector_1_access_2),
    .request(player_thread_1_request), .collide(collide));
  Button button_1 (.out(shot));
  Multiplexer #(.width(3), .enable("false")) multiplexer_1 (
    .in0(3'b100), .in1(3'b010), .out(multiplexer_1_out), .sel(button_2_out));
  drawer drawer_3 (
    .out_6(drawer_3_out_6), .out_8(drawer_3_out_8), .out_9(drawer_3_out_9), .out_10(drawer_3_out_10),
    .in_1(bullet_thread_1_id), .in_2(bullet_thread_1_x), .in_3(bullet_thread_1_y),
    .in_4(bullet_thread_1_command), .out_7(drawer_3_out_7), .clk(clk));
  bullet_thread bullet_thread_1 (
    .run(run), .drawing(drawer_3_out_6), .clk(clk), .collided(collide), .end_cycle(end_cycle),
    .id(bullet_thread_1_id), .x(bullet_thread_1_x), .y(bullet_thread_1_y), .command(bullet_thread_1_command),
    .adr(main_thread_1_adr), .val(main_thread_1_val), .write(main_thread_1_write),
    .collide_check_player(collide_check_player), .collide_check_enemy(collide_check_enemy),
    .collide_check_wall(collide_check_wall), .x_col(x_col), .y_col(y_col));
  Button button_2 (.out(button_2_out));
  Button button_3 (.out(button_3_out));
  Transistor #(.width(3)) transistor_1 (.in(multiplexer_1_out), .out(x_vec), .gate(button_3_out));
  Comparator #(.width(6), .mode("unsigned")) comparator_1 ();  // open: a, b, gt, eq, lt
  Comparator #(.width(6), .mode("unsigned")) comparator_2 ();  // open: a, b, gt, eq, lt
  Comparator #(.width(6), .mode("unsigned")) comparator_3 ();  // open: a, b, gt, eq, lt
  Comparator #(.width(6), .mode("unsigned")) comparator_4 ();  // open: a, b, gt, eq, lt
  Transistor #(.width(3)) transistor_2 (.in(multiplexer_2_out), .out(x_vec), .gate(button_2_out));
  Multiplexer #(.width(3), .enable("false")) multiplexer_2 (
    .in0(3'b100), .in1(3'b110), .out(multiplexer_2_out), .sel(button_3_out));
  Register #(.width(16)) x (.D(main_thread_1_val));  // open: en, Q, clk, clr
  Register #(.width(16)) y (.D(main_thread_1_val));  // open: en, Q, clk, clr
  Register #(.width(16)) \rand  (.D(main_thread_1_val));  // open: en, Q, clk, clr
  Register #(.width(16)) register_1 (.D(main_thread_1_val));  // open: en, Q, clk, clr
  Hex_Digit_Display hex_digit_display_1 (.value(bit_extender_1_out));  // open: dp
  Bit_Extender #(.in_width(16), .out_width(4)) bit_extender_1 (.in(hp), .out(bit_extender_1_out));
  Hex_Digit_Display hex_digit_display_2 (.value(bit_extender_3_out));  // open: dp
  Hex_Digit_Display hex_digit_display_3 (.value(bit_extender_2_out));  // open: dp
  Divider #(.width(16)) divider_1 (.a(score), .b(16'ha), .out(divider_1_out), .rem(divider_1_rem));  // open: upper
  Divider #(.width(16)) divider_2 (.a(divider_1_out), .b(16'ha), .rem(divider_2_rem));  // open: out, upper
  Bit_Extender #(.in_width(16), .out_width(4)) bit_extender_2 (.in(divider_2_rem), .out(bit_extender_2_out));
  Bit_Extender #(.in_width(16), .out_width(4)) bit_extender_3 (.in(divider_1_rem), .out(bit_extender_3_out));

  // Notes on the sheet:
  //   Shoot
  //   Movement
  //   <-
  //   ->
  //   HP
  //   SCORE
endmodule

module CDM16 (
  input  [15:0] adr,
  input  [15:0] val,
  input  clock,
  input  write,
  input  hold,
  input  end_cycle,
  output holded,
  output drawing,
  output [15:0] id,
  output [15:0] x,
  output [15:0] y,
  output [15:0] command,
  output collide,
  output wait_int__checker,
  output run,
  output [15:0] score,
  output button,
  output gg,
  output win,
  output [15:0] hp
);

  wire and_2_out, and_3_out, and_4_out, and_5_out, and_6_out, and_7_out, and_8_out, and_9_out, and_10_out,
       and_11_out, and_12_out, and_13_out, and_14_out, and_15_out, and_16_out, bit_extender_1_out,
       cdm_16_1_p3, cdm_16_1_p4, code, comparator_3_eq, comparator_5_eq, comparator_7_eq, comparator_8_eq,
       comparator_9_eq, comparator_12_eq, comparator_13_eq, comparator_15_eq, data, decoder_1_out0,
       decoder_1_out1, initialized, mem, not_1_out, not_2_out, not_3_out, not_4_out, not_7_out, or_1_out,
       or_2_out, pull_resistor_5_node, pull_resistor_6_node, pull_resistor_8_node, pull_resistor_10_node,
       pull_resistor_14_node, pull_resistor_15_node, pull_resistor_17_node, read_write, transistor_3_out,
       transistor_6_out, word, write_t;
  wire [15:0] cdm_16_1_p8, cdm_16_1_p9, cdm_16_1_p10, controlled_buffer_2_out, register_1_q, register_2_q,
       register_3_q, register_4_q, register_5_q, register_6_q, register_7_q, register_9_q, register_10_q,
       register_11_q, transistor_4_out;

  // Debugger debugger_1: pin names not known
  and and_1 (write_t, write, holded);
  D_Flip_Flop #(.trigger("falling")) d_ff_1 (.clk(clock), .D(or_1_out), .Q(holded));  // open: Qn, preset, en, reset
  or or_1 (or_1_out, write, and_2_out, or_2_out);
  buf or_2 (or_2_out, hold);  // OR_Gate
  and and_2 (and_2_out, ~initialized, wait_int__checker);  // AND_Gate
  // CdM_16 cdm_16_1: pin names not known; wires that end beside it: holded, clock, cdm_16_1_p3, cdm_16_1_p4, mem, read_write, word, cdm_16_1_p8, cdm_16_1_p9, cdm_16_1_p10
  // Probe on cdm_16_1_p3
  not not_1 (not_1_out, write_t);
  not not_2 (not_2_out, write_t);
  assign cdm_16_1_p10 = and_4_out ? controlled_buffer_2_out : 16'bz;  // Controlled_Buffer controlled_buffer_1
  assign controlled_buffer_2_out = and_3_out ? cdm_16_1_p9 : 16'bz;  // Controlled_Buffer controlled_buffer_2
  and and_3 (and_3_out, not_1_out, not_3_out);
  not not_3 (not_3_out, read_write);
  not not_4 (not_4_out, read_write);
  and and_4 (and_4_out, not_2_out, read_write);
  Pull_Resistor pull_resistor_1 (.node(code));
  Transistor transistor_1 (.in(decoder_1_out0), .out(code), .gate(write_t));
  Transistor #(.gate("br")) transistor_2 (.in(decoder_1_out1), .out(data), .gate(write_t));
  Pull_Resistor #(.pull(1)) pull_resistor_2 (.node(data));
  Decoder #(.disabled(0)) decoder_1 (.out0(decoder_1_out0), .out1(decoder_1_out1), .sel(cdm_16_1_p4), .en(mem));
  Transistor transistor_3 (.in(not_4_out), .out(transistor_3_out), .gate(write_t));
  Pull_Resistor #(.pull(1)) pull_resistor_3 (.node(transistor_3_out));
  Transistor #(.\type ("n"), .width(16)) transistor_4 (.in(adr), .out(transistor_4_out), .gate(write_t));
  Transistor #(.gate("br"), .width(16)) transistor_5 (.in(cdm_16_1_p8), .out(transistor_4_out), .gate(write_t));
  // Probe on transistor_4_out
  Transistor transistor_6 (.in(word), .out(transistor_6_out), .gate(write_t));
  Pull_Resistor #(.pull(1)) pull_resistor_4 (.node(transistor_6_out));
  Pull_Resistor pull_resistor_5 (.node(pull_resistor_5_node));
  Comparator #(.width(16)) comparator_1 (.a(transistor_4_out), .b(16'h86), .eq(pull_resistor_5_node));  // open: gt, lt
  Pull_Resistor pull_resistor_6 (.node(pull_resistor_6_node));
  Comparator #(.width(16)) comparator_2 (.a(transistor_4_out), .b(16'h88), .eq(pull_resistor_6_node));  // open: gt, lt
  Comparator #(.width(16)) comparator_3 (.a(transistor_4_out), .b(16'h8a), .eq(comparator_3_eq));  // open: gt, lt
  Pull_Resistor pull_resistor_7 (.node(comparator_3_eq));
  Pull_Resistor pull_resistor_8 (.node(pull_resistor_8_node));
  Comparator #(.width(16)) comparator_4 (.a(transistor_4_out), .b(16'h8c), .eq(pull_resistor_8_node));  // open: gt, lt
  Comparator #(.width(16)) comparator_5 (.a(transistor_4_out), .b(16'h94), .eq(comparator_5_eq));  // open: gt, lt
  Pull_Resistor pull_resistor_9 (.node(comparator_5_eq));
  Pull_Resistor pull_resistor_10 (.node(pull_resistor_10_node));
  Comparator #(.width(16)) comparator_6 (.a(transistor_4_out), .b(16'h84), .eq(pull_resistor_10_node));  // open: gt, lt
  Comparator #(.width(16)) comparator_7 (.a(transistor_4_out), .b(16'h96), .eq(comparator_7_eq));  // open: gt, lt
  Pull_Resistor pull_resistor_11 (.node(comparator_7_eq));
  Comparator #(.width(16)) comparator_8 (.a(transistor_4_out), .b(16'h9e), .eq(comparator_8_eq));  // open: gt, lt
  Pull_Resistor pull_resistor_12 (.node(comparator_8_eq));
  Comparator #(.width(16)) comparator_9 (.a(transistor_4_out), .b(16'ha0), .eq(comparator_9_eq));  // open: gt, lt
  Pull_Resistor pull_resistor_13 (.node(comparator_9_eq));
  Pull_Resistor pull_resistor_14 (.node(pull_resistor_14_node));
  Comparator #(.width(16)) comparator_10 (
    .a(transistor_4_out), .b(16'h9c), .eq(pull_resistor_14_node));  // open: gt, lt
  Pull_Resistor pull_resistor_15 (.node(pull_resistor_15_node));
  Comparator #(.width(16)) comparator_11 (
    .a(transistor_4_out), .b(16'hae), .eq(pull_resistor_15_node));  // open: gt, lt
  Comparator #(.width(16)) comparator_12 (.a(transistor_4_out), .b(16'hb0), .eq(comparator_12_eq));  // open: gt, lt
  Pull_Resistor pull_resistor_16 (.node(comparator_12_eq));
  Pull_Resistor pull_resistor_17 (.node(pull_resistor_17_node));
  Transistor #(.gate("br")) transistor_7 (.in(read_write), .out(pull_resistor_17_node), .gate(write_t));
  // ROM rom_1: pin names not known; wires that end beside it: transistor_4_out, code, word, controlled_buffer_2_out
  // RAM ram_1: pin names not known; wires that end beside it: transistor_4_out, transistor_6_out, data, clock, pull_resistor_17_node, controlled_buffer_2_out
  Register #(.width(16)) register_1 (.D(controlled_buffer_2_out), .Q(register_1_q), .clk(and_5_out));  // open: en, clr
  and and_5 (and_5_out, pull_resistor_5_node, data, transistor_3_out);
  Register #(.width(16)) register_2 (.D(controlled_buffer_2_out), .Q(register_2_q), .clk(and_6_out));  // open: en, clr
  and and_6 (and_6_out, pull_resistor_6_node, data, transistor_3_out);
  Register #(.width(16)) register_3 (.D(controlled_buffer_2_out), .Q(register_3_q), .clk(and_7_out));  // open: en, clr
  and and_7 (and_7_out, comparator_3_eq, data, transistor_3_out);
  Register #(.width(16)) register_4 (.D(controlled_buffer_2_out), .Q(register_4_q), .clk(and_8_out));  // open: en, clr
  and and_8 (and_8_out, pull_resistor_8_node, data, transistor_3_out);
  Register #(.width(16)) register_5 (.D(controlled_buffer_2_out), .Q(register_5_q), .clk(and_9_out));  // open: en, clr
  and and_9 (and_9_out, comparator_5_eq, data, transistor_3_out);
  Register #(.width(16)) register_6 (
    .D(controlled_buffer_2_out), .Q(register_6_q), .clk(and_10_out), .clr(end_cycle));  // open: en
  and and_10 (and_10_out, pull_resistor_10_node, data, transistor_3_out);
  Register #(.width(16)) register_7 (.D(controlled_buffer_2_out), .Q(register_7_q), .clk(and_11_out));  // open: en, clr
  and and_11 (and_11_out, comparator_7_eq, data, transistor_3_out);
  Register #(.width(16)) register_8 (.D(controlled_buffer_2_out), .Q(score), .clk(and_12_out));  // open: en, clr
  and and_12 (and_12_out, comparator_8_eq, data, transistor_3_out);
  Register #(.width(16)) register_9 (.D(controlled_buffer_2_out), .Q(register_9_q), .clk(and_13_out));  // open: en, clr
  and and_13 (and_13_out, comparator_9_eq, data, transistor_3_out);
  Register #(.width(16)) register_10 (
    .D(controlled_buffer_2_out), .Q(register_10_q), .clk(and_14_out));  // open: en, clr
  and and_14 (and_14_out, pull_resistor_14_node, data, transistor_3_out);
  Register #(.width(16)) register_11 (
    .D(controlled_buffer_2_out), .Q(register_11_q), .clk(and_15_out));  // open: en, clr
  and and_15 (and_15_out, pull_resistor_15_node, data, transistor_3_out);
  Register #(.width(16)) register_12 (.D(controlled_buffer_2_out), .Q(hp), .clk(and_16_out));  // open: en, clr
  and and_16 (and_16_out, comparator_12_eq, data, transistor_3_out);
  Transistor #(.\type ("n"), .width(16)) transistor_8 (.in(val), .out(controlled_buffer_2_out), .gate(write_t));
  assign id = drawing ? register_1_q : 16'bz;  // Controlled_Buffer controlled_buffer_3
  assign x = drawing ? register_2_q : 16'bz;  // Controlled_Buffer controlled_buffer_4
  assign y = drawing ? register_3_q : 16'bz;  // Controlled_Buffer controlled_buffer_5
  assign command = drawing ? register_4_q : 16'bz;  // Controlled_Buffer controlled_buffer_6
  Comparator #(.width(16), .mode("unsigned")) comparator_13 (
    .a(register_5_q), .b({16{1'b0}}), .eq(comparator_13_eq));  // open: gt, lt
  Bit_Extender #(.in_width(16), .out_width(1)) bit_extender_1 (.in(register_7_q), .out(bit_extender_1_out));
  Bit_Extender #(.in_width(16), .out_width(1)) bit_extender_2 (.in(register_9_q), .out(button));
  Bit_Extender #(.in_width(16), .out_width(1)) bit_extender_3 (.in(register_10_q), .out(gg));
  Bit_Extender #(.in_width(16), .out_width(1)) bit_extender_4 (.in(register_11_q), .out(win));
  not not_5 (collide, comparator_13_eq);
  Comparator #(.width(16), .mode("unsigned")) comparator_14 (
    .a(register_6_q), .b(16'h2), .eq(drawing));  // open: gt, lt
  Comparator #(.width(16), .mode("unsigned")) comparator_15 (
    .a(register_6_q), .b({16{1'b0}}), .eq(comparator_15_eq));  // open: gt, lt
  not not_6 (wait_int__checker, comparator_15_eq);
  not not_7 (not_7_out, drawing);
  xor xor_1 (run, not_7_out, bit_extender_1_out);
  Register #(.width(1)) u_initialized (.D(run), .Q(initialized), .clk(run));  // open: en, clr

  // Other names for the same wires on the sheet: checker = wait_int__checker; cl = clock; draw = drawing;
  //   end = end_cycle

  // Notes on the sheet:
  //   hold приостанавливает процессор
  //   write как hold но даёт возможность писать в ОЗУ
  //   cheker
  //   run
endmodule

module main_thread (
  input  [15:0] id,
  input  [15:0] x,
  input  [15:0] y,
  input  [15:0] command,
  input  response,
  input  write_sync,
  input  end_cycle,
  input  clock,
  input  drawing,
  input  processor_drawing,
  input  run,
  input  [15:0] x_col,
  input  wait_int,
  input  [15:0] y_col,
  input  collide_check_enemy,
  input  collide_check_wall,
  input  win,
  input  lose,
  output [4:0] X_2,
  output [4:0] Y_2,
  output [15:0] ID_2,
  output [15:0] Command_2,
  output hold,
  output request,
  output write,
  output [15:0] val,
  output [15:0] adr,
  output draw,
  output collide
);

  wire and_1_out, and_2_out, comparator_5_eq, comparator_6_eq, enemies_multiobject_1_ready, enemy_initing,
       int_enemy, int_player, not_1_out, not_2_out, processor_draw, pull_resistor_3_node,
       pull_resistor_6_node, register_1_q, requester_1_permission_received, requester_2_permission_received,
       requester_3_permission_received, save_pos, \wait , wall_initing, wall_multiobject_1_initing,
       wall_multiobject_1_ready, wall_multiobject_2_initing, wall_multiobject_2_ready,
       wall_multiobject_3_initing;
  wire [4:0] enemies_multiobject_1_debug__enemy_cout, wall_multiobject_1_debug__wall_cout,
       wall_multiobject_2_debug__wall_cout, wall_multiobject_3_debug__wall_cout;
  wire [5:0] enemies_multiobject_1_proc_command;
  wire [15:0] collided, divider_1_out, divider_2_out, register_2_q;

  or or_1 (hold, wall_initing, enemy_initing, processor_drawing);
  or or_2 (\wait , wait_int, request, drawing);
  Pull_Resistor pull_resistor_1 (.node(collided));
  // Probe on enemies_multiobject_1_debug__enemy_cout
  Comparator #(.width(16), .mode("unsigned")) comparator_1 (.a(command), .b(16'h1), .eq(draw));  // open: gt, lt
  Pull_Resistor pull_resistor_2 (.node(draw));
  Pull_Resistor pull_resistor_3 (.node(pull_resistor_3_node));
  Comparator #(.width(16), .mode("unsigned")) comparator_2 (
    .a(command), .b(16'h2), .eq(pull_resistor_3_node));  // open: gt, lt
  Comparator #(.width(6), .mode("unsigned")) comparator_3 (
    .a(enemies_multiobject_1_proc_command), .b({6{1'b0}}), .eq(int_player));  // open: gt, lt
  Pull_Resistor pull_resistor_4 (.node(int_player));
  Pull_Resistor pull_resistor_5 (.node(int_enemy));
  Comparator #(.width(6), .mode("unsigned")) comparator_4 (
    .a(enemies_multiobject_1_proc_command), .b(6'b000001), .eq(int_enemy));  // open: gt, lt
  enemies_multiobject enemies_multiobject_1 (
    .\wait (\wait ), .draw(run), .id(id), .y(y), .x(x), .command(command),
    .ready(enemies_multiobject_1_ready), .initing(enemy_initing), .collide_check(collide_check_enemy),
    .clock(clock), .DEBUG__enemy_cout(enemies_multiobject_1_debug__enemy_cout),
    .proc_command(enemies_multiobject_1_proc_command), .end_cycle(end_cycle), .x_col(x_col), .y_col(y_col),
    .collided(collided));  // open: speed
  // Probe on wall_multiobject_1_debug__wall_cout
  wall_multiobject wall_multiobject_1 (
    .\wait (\wait ), .draw(enemies_multiobject_1_ready), .x_col(x_col), .y_col(y_col), .id(id), .y(y), .x(x),
    .command(command), .ready(wall_multiobject_1_ready), .end_cycle(end_cycle),
    .collide_check(collide_check_wall), .collided(collided),
    .DEBUG__wall_cout(wall_multiobject_1_debug__wall_cout), .initing(wall_multiobject_1_initing),
    .clock(clock), .start_x(16'h8), .start_y(16'h32));
  Register #(.width(1)) register_1 (
    .D(processor_draw), .Q(register_1_q), .clk(processor_draw), .clr(and_1_out));  // open: en
  Pull_Resistor pull_resistor_6 (.node(pull_resistor_6_node));
  or or_3 (wall_initing, wall_multiobject_1_initing, wall_multiobject_2_initing, wall_multiobject_3_initing);
  // Probe on wall_multiobject_2_debug__wall_cout
  wall_multiobject wall_multiobject_2 (
    .\wait (\wait ), .draw(wall_multiobject_1_ready), .x_col(x_col), .y_col(y_col), .id(id), .y(y), .x(x),
    .command(command), .ready(wall_multiobject_2_ready), .end_cycle(end_cycle),
    .collide_check(collide_check_wall), .collided(collided),
    .DEBUG__wall_cout(wall_multiobject_2_debug__wall_cout), .initing(wall_multiobject_2_initing),
    .clock(clock), .start_x(16'h1c), .start_y(16'h32));
  and and_1 (and_1_out, ~drawing, register_1_q);  // AND_Gate
  Pull_Resistor pull_resistor_7 (.node(request));
  requester requester_1 (
    .make_request(and_1_out), .permission_received(requester_1_permission_received),
    .writing_data(pull_resistor_6_node), .request(request), .response(response));
  check2_writer check2_writer_1 (
    .adr(adr), .val(val), .write(pull_resistor_6_node), .run(requester_1_permission_received), .clock(clock),
    .sync(write_sync));
  // Probe on wall_multiobject_3_debug__wall_cout
  wall_multiobject wall_multiobject_3 (
    .\wait (\wait ), .draw(wall_multiobject_2_ready), .x_col(x_col), .y_col(y_col), .id(id), .y(y), .x(x),
    .command(command), .ready(processor_draw), .end_cycle(end_cycle), .collide_check(collide_check_wall),
    .collided(collided), .DEBUG__wall_cout(wall_multiobject_3_debug__wall_cout),
    .initing(wall_multiobject_3_initing), .clock(clock), .start_x(16'h30), .start_y(16'h32));
  not not_1 (not_1_out, comparator_5_eq);
  Comparator #(.width(16), .mode("unsigned")) comparator_5 (
    .a(collided), .b({16{1'b0}}), .eq(comparator_5_eq));  // open: gt, lt
  Register #(.width(16)) register_2 (.D(collided), .Q(register_2_q), .clk(not_1_out));  // open: en, clr
  requester requester_2 (
    .make_request(not_1_out), .permission_received(requester_2_permission_received),
    .writing_data(pull_resistor_6_node), .request(request), .response(response));
  collision_writer collision_writer_1 (
    .adr(adr), .val(val), .write(pull_resistor_6_node), .run(requester_2_permission_received), .clock(clock),
    .collided(register_2_q));
  // Probe on id
  // Probe on x
  // Probe on y
  // Probe on command
  Divider #(.width(16)) divider_1 (.a(x), .b(16'h2), .out(divider_1_out));  // open: upper, rem
  and and_2 (and_2_out, draw, int_enemy);
  and and_3 (save_pos, draw, int_player);
  // Probe on X_2
  Bit_Extender #(.in_width(16), .out_width(5)) bit_extender_1 (.in(divider_1_out), .out(X_2));
  Divider #(.width(16)) divider_2 (.a(y), .b(16'h2), .out(divider_2_out));  // open: upper, rem
  requester requester_3 (
    .make_request(and_2_out), .permission_received(requester_3_permission_received),
    .writing_data(pull_resistor_6_node), .request(request), .response(response));
  Comparator #(.width(16), .mode("unsigned")) comparator_6 (
    .a(collided), .b({16{1'b0}}), .eq(comparator_6_eq));  // open: gt, lt
  // Probe on Y_2
  Bit_Extender #(.in_width(16), .out_width(5)) bit_extender_2 (.in(divider_2_out), .out(Y_2));
  win_multiobject win_multiobject_1 (
    .\wait (\wait ), .draw(win), .id(id), .x(x), .y(y), .command(command), .clock(clock));  // open: ready
  enemy_writer enemy_writer_1 (
    .x(x), .y(y), .adr(adr), .val(val), .write(pull_resistor_6_node), .clock(clock),
    .run(requester_3_permission_received));
  not not_2 (not_2_out, comparator_6_eq);
  buf buffer_1 (collide, not_2_out);
  lose_multiobject lose_multiobject_1 (
    .\wait (\wait ), .draw(lose), .id(id), .x(x), .y(y), .command(command), .clock(clock));  // open: ready
  buf buffer_2 (write, pull_resistor_6_node);

  assign Command_2 = command;
  assign ID_2 = id;

  // Other names for the same wires on the sheet: clk = clock; command_draw = draw

  // Notes on the sheet:
  //   response: pull=down
  //   buffer_1 drives only 1 and floats otherwise
  //   buffer_2 drives only 1 and floats otherwise
endmodule

module player_thread (
  input  [2:0] px,
  input  shot,
  input  drawing,
  input  clk,
  input  run,
  input  response,
  input  end_cycle,
  input  collide_check_player,
  input  button,
  output [15:0] id,
  output [4:0] x,
  output [15:0] command,
  output [4:0] y,
  output [15:0] val,
  output [15:0] adr,
  output request,
  output write,
  output collide
);

  wire and_1_out, and_2_out, command_draw, comparator_1_eq, comparator_3_eq, comparator_4_eq,
       counter_1_carry, cycle, d_ff_1_qn, d_ff_2_qn, not_1_out, not_2_out, not_3_out, player_initing,
       player_multiobject_1_ready, pull_resistor_3_node, register_1_q, register_2_q,
       requester_1_permission_received, requester_2_permission_received, \wait , xor_1_out;
  wire [15:0] bit_extender_1_out, collided, player_multiobject_1_x_2, player_multiobject_1_y, register_3_q,
       register_4_q, register_5_q, shifter_1_out, shifter_2_out, subtractor_1_out, x_col, y_col;

  assign bit_extender_1_out = {{13{1'b0}}, px};  // Bit_Extender bit_extender_1
  Subtractor #(.width(16)) subtractor_1 (.a(bit_extender_1_out), .b(16'h4), .out(subtractor_1_out));  // open: bin, bout
  or or_1 (\wait , drawing, request);
  Counter #(.width(2), .max('h3)) counter_1 (
    .carry(counter_1_carry), .clk(clk), .clr(d_ff_1_qn));  // open: load, D, count, Q
  D_Flip_Flop d_ff_1 (.clk(cycle), .D(cycle), .Qn(d_ff_1_qn), .reset(counter_1_carry));  // open: Q, preset, en
  not not_1 (not_1_out, comparator_1_eq);
  Comparator #(.width(16), .mode("unsigned")) comparator_1 (
    .a({16{1'b0}}), .b(subtractor_1_out), .eq(comparator_1_eq));  // open: gt, lt
  and and_1 (and_1_out, counter_1_carry, not_1_out);
  Register #(.width(1)) register_1 (.D(not_1_out), .Q(register_1_q), .clk(not_1_out), .clr(register_1_q));  // open: en
  Pull_Resistor pull_resistor_1 (.node(button));
  ExactlyOne xor_1 (.out(xor_1_out), .in0(run), .in1(and_1_out), .in2(register_1_q));
  player_multiobject player_multiobject_1 (
    .draw(xor_1_out), .ready(player_multiobject_1_ready), .id(id), .x_2(player_multiobject_1_x_2),
    .y(player_multiobject_1_y), .x(subtractor_1_out), .command(command), .\wait (\wait ), .clock(clk),
    .initing(player_initing), .end_cycle(end_cycle), .x_col(x_col), .y_col(y_col),
    .collide_check(collide_check_player), .collided(collided));
  Comparator #(.width(16), .mode("unsigned")) comparator_2 (.a(command), .b(16'h1), .eq(command_draw));  // open: gt, lt
  Pull_Resistor pull_resistor_2 (.node(command_draw));
  Register #(.width(1)) register_2 (.D(shot), .Q(register_2_q), .clk(shot), .clr(and_2_out));  // open: en
  Counter #(.width(2), .max('h3)) counter_2 (.carry(cycle), .clk(clk), .clr(d_ff_2_qn));  // open: load, D, count, Q
  D_Flip_Flop d_ff_2 (
    .clk(player_multiobject_1_ready), .D(player_multiobject_1_ready), .Qn(d_ff_2_qn), .reset(cycle));  // open: Q, preset, en
  and and_2 (and_2_out, register_2_q, ~button);  // AND_Gate
  Register #(.width(16)) register_3 (
    .D(player_multiobject_1_y), .Q(register_3_q), .clk(command_draw));  // open: en, clr
  Register #(.width(16)) register_4 (
    .D(player_multiobject_1_x_2), .Q(register_4_q), .clk(command_draw));  // open: en, clr
  requester requester_1 (
    .make_request(and_2_out), .permission_received(requester_1_permission_received),
    .writing_data(pull_resistor_3_node), .request(request), .response(response));
  Pull_Resistor pull_resistor_3 (.node(pull_resistor_3_node));
  Bit_Extender #(.in_width(16), .out_width(5)) bit_extender_2 (.in(shifter_1_out), .out(x));
  Shifter #(.width(16), .shift("lr")) shifter_1 (.in(player_multiobject_1_x_2), .\dist (4'b0001), .out(shifter_1_out));
  shot_writer shot_writer_1 (
    .adr(adr), .val(val), .run(requester_1_permission_received), .write(pull_resistor_3_node), .clock(clk),
    .x(register_4_q), .y(register_3_q));
  Bit_Extender #(.in_width(16), .out_width(5)) bit_extender_3 (.in(shifter_2_out), .out(y));
  Shifter #(.width(16), .shift("lr")) shifter_2 (.in(player_multiobject_1_y), .\dist (4'b0001), .out(shifter_2_out));
  Register #(.width(16)) register_5 (.D(collided), .Q(register_5_q), .clk(not_2_out));  // open: en, clr
  not not_2 (not_2_out, comparator_3_eq);
  Comparator #(.width(16), .mode("unsigned")) comparator_3 (
    .a(collided), .b({16{1'b0}}), .eq(comparator_3_eq));  // open: gt, lt
  Comparator #(.width(16), .mode("unsigned")) comparator_4 (
    .a(collided), .b({16{1'b0}}), .eq(comparator_4_eq));  // open: gt, lt
  requester requester_2 (
    .make_request(not_2_out), .permission_received(requester_2_permission_received));  // open: writing_data, request, response
  collision_writer collision_writer_1 (
    .adr(adr), .val(val), .write(pull_resistor_3_node), .run(requester_2_permission_received), .clock(clk),
    .collided(register_5_q));
  buf buffer_1 (collide, not_3_out);
  not not_3 (not_3_out, comparator_4_eq);
  Pull_Resistor pull_resistor_4 (.node(request));
  Pull_Resistor pull_resistor_5 (.node(collided));
  buf buffer_2 (write, pull_resistor_3_node);

  // Notes on the sheet:
  //   buffer_1 drives only 1 and floats otherwise
  //   buffer_2 drives only 1 and floats otherwise
endmodule

module _32buffer_el (
  input  [31:0] \input ,
  input  _1___buffer_read,
  input  _1___buffer_write___clr,
  output [31:0] video
);

  wire [31:0] buffer_q, or_1_out;

  assign or_1_out = \input  | buffer_q;  // OR_Gate or_1, 32 bits wide
  Register #(.width(32)) buffer (
    .D(or_1_out), .Q(buffer_q), .clk(_1___buffer_read), .clr(_1___buffer_write___clr));  // open: en
  Register #(.width(32)) u_video (.D(buffer_q), .Q(video), .clk(_1___buffer_write___clr));  // open: en, clr
endmodule

module _32video_buffer_extendable (
  input  [31:0] in_1,
  input  w,
  input  block,
  input  [4:0] y,
  output [31:0] out_5,
  output [31:0] out_6,
  output [31:0] out_7,
  output [31:0] out_8,
  output [31:0] out_9,
  output [31:0] out_10,
  output [31:0] out_11,
  output [31:0] out_12,
  output [31:0] out_13,
  output [31:0] out_14,
  output [31:0] out_15,
  output [31:0] out_16,
  output [31:0] out_17,
  output [31:0] out_18,
  output [31:0] out_19,
  output [31:0] out_20,
  output [31:0] out_21,
  output [31:0] out_22,
  output [31:0] out_23,
  output [31:0] out_24,
  output [31:0] out_25,
  output [31:0] out_26,
  output [31:0] out_27,
  output [31:0] out_28,
  output [31:0] out_29,
  output [31:0] out_30,
  output [31:0] out_31,
  output [31:0] out_32,
  output [31:0] out_33,
  output [31:0] out_34,
  output [31:0] out_35,
  output [31:0] out_36
);

  wire _0, _1, _2, _3, _4, _5, _6, _7, _8, _9, _10, _11, _12, _13, _14, _15, _16, _17, _18, _19, _20, _21,
       _22, _23, _24, _25, _26, _27, _28, _29, _30, _31, clock_1_out, nor_1_out;

  Demultiplexer #(.select(5), .disabled(0)) demultiplexer_1 (
    .out0(_0), .out1(_1), .out2(_2), .out3(_3), .out4(_4), .out5(_5), .out6(_6), .out7(_7), .out8(_8),
    .out9(_9), .out10(_10), .out11(_11), .out12(_12), .out13(_13), .out14(_14), .out15(_15), .out16(_16),
    .out17(_17), .out18(_18), .out19(_19), .out20(_20), .out21(_21), .out22(_22), .out23(_23), .out24(_24),
    .out25(_25), .out26(_26), .out27(_27), .out28(_28), .out29(_29), .out30(_30), .out31(_31), .in(1'b1),
    .sel(y), .en(nor_1_out));
  nor nor_1 (nor_1_out, block, clock_1_out);
  Clock clock_1 (.out(clock_1_out));
  _32buffer_el u_32buffer_el_1 (.\input (in_1), ._1___buffer_read(_0), .video(out_5), ._1___buffer_write___clr(w));
  _32buffer_el u_32buffer_el_2 (.\input (in_1), ._1___buffer_read(_1), .video(out_6), ._1___buffer_write___clr(w));
  _32buffer_el u_32buffer_el_3 (.\input (in_1), ._1___buffer_read(_2), .video(out_7), ._1___buffer_write___clr(w));
  _32buffer_el u_32buffer_el_4 (.\input (in_1), ._1___buffer_read(_3), .video(out_8), ._1___buffer_write___clr(w));
  _32buffer_el u_32buffer_el_5 (.\input (in_1), ._1___buffer_read(_4), .video(out_9), ._1___buffer_write___clr(w));
  _32buffer_el u_32buffer_el_6 (.\input (in_1), ._1___buffer_read(_5), .video(out_10), ._1___buffer_write___clr(w));
  _32buffer_el u_32buffer_el_7 (.\input (in_1), ._1___buffer_read(_6), .video(out_11), ._1___buffer_write___clr(w));
  _32buffer_el u_32buffer_el_8 (.\input (in_1), ._1___buffer_read(_7), .video(out_12), ._1___buffer_write___clr(w));
  _32buffer_el u_32buffer_el_9 (.\input (in_1), ._1___buffer_read(_8), .video(out_13), ._1___buffer_write___clr(w));
  _32buffer_el u_32buffer_el_10 (.\input (in_1), ._1___buffer_read(_9), .video(out_14), ._1___buffer_write___clr(w));
  _32buffer_el u_32buffer_el_11 (.\input (in_1), ._1___buffer_read(_10), .video(out_15), ._1___buffer_write___clr(w));
  _32buffer_el u_32buffer_el_12 (.\input (in_1), ._1___buffer_read(_11), .video(out_16), ._1___buffer_write___clr(w));
  _32buffer_el u_32buffer_el_13 (.\input (in_1), ._1___buffer_read(_12), .video(out_17), ._1___buffer_write___clr(w));
  _32buffer_el u_32buffer_el_14 (.\input (in_1), ._1___buffer_read(_13), .video(out_18), ._1___buffer_write___clr(w));
  _32buffer_el u_32buffer_el_15 (.\input (in_1), ._1___buffer_read(_14), .video(out_19), ._1___buffer_write___clr(w));
  _32buffer_el u_32buffer_el_16 (.\input (in_1), ._1___buffer_read(_15), .video(out_20), ._1___buffer_write___clr(w));
  _32buffer_el u_32buffer_el_17 (.\input (in_1), ._1___buffer_read(_16), .video(out_21), ._1___buffer_write___clr(w));
  _32buffer_el u_32buffer_el_18 (.\input (in_1), ._1___buffer_read(_17), .video(out_22), ._1___buffer_write___clr(w));
  _32buffer_el u_32buffer_el_19 (.\input (in_1), ._1___buffer_read(_18), .video(out_23), ._1___buffer_write___clr(w));
  _32buffer_el u_32buffer_el_20 (.\input (in_1), ._1___buffer_read(_19), .video(out_24), ._1___buffer_write___clr(w));
  _32buffer_el u_32buffer_el_21 (.\input (in_1), ._1___buffer_read(_20), .video(out_25), ._1___buffer_write___clr(w));
  _32buffer_el u_32buffer_el_22 (.\input (in_1), ._1___buffer_read(_21), .video(out_26), ._1___buffer_write___clr(w));
  _32buffer_el u_32buffer_el_23 (.\input (in_1), ._1___buffer_read(_22), .video(out_27), ._1___buffer_write___clr(w));
  _32buffer_el u_32buffer_el_24 (.\input (in_1), ._1___buffer_read(_23), .video(out_28), ._1___buffer_write___clr(w));
  _32buffer_el u_32buffer_el_25 (.\input (in_1), ._1___buffer_read(_24), .video(out_29), ._1___buffer_write___clr(w));
  _32buffer_el u_32buffer_el_26 (.\input (in_1), ._1___buffer_read(_25), .video(out_30), ._1___buffer_write___clr(w));
  _32buffer_el u_32buffer_el_27 (.\input (in_1), ._1___buffer_read(_26), .video(out_31), ._1___buffer_write___clr(w));
  _32buffer_el u_32buffer_el_28 (.\input (in_1), ._1___buffer_read(_27), .video(out_32), ._1___buffer_write___clr(w));
  _32buffer_el u_32buffer_el_29 (.\input (in_1), ._1___buffer_read(_28), .video(out_33), ._1___buffer_write___clr(w));
  _32buffer_el u_32buffer_el_30 (.\input (in_1), ._1___buffer_read(_29), .video(out_34), ._1___buffer_write___clr(w));
  _32buffer_el u_32buffer_el_31 (.\input (in_1), ._1___buffer_read(_30), .video(out_35), ._1___buffer_write___clr(w));
  _32buffer_el u_32buffer_el_32 (.\input (in_1), ._1___buffer_read(_31), .video(out_36), ._1___buffer_write___clr(w));

  // Other names for the same wires on the sheet: inp[31:0] = in_1

  // Notes on the sheet:
  //   block: pull=down
endmodule

module _32x32_ball (
  input  [5:0] in_1,
  input  [5:0] in_2,
  input  in_3,
  input  [4:0] in_4,
  output [31:0] out_5
);

  wire and_1_out, and_2_out, and_3_out, clock_1_out, clock_2_out, counter_1_q, counter_2_q, nor_1_out,
       nor_2_out, or_1_out, or_2_out;
  wire [4:0] bit_extender_1_out, bit_extender_2_out, xnor_1_out;
  wire [5:0] adder_1_out, adder_2_out, negator_1_out, negator_2_out, transistor_1_out, transistor_3_out, x_q,
       xv_q, y_q, yv_q;
  wire [31:0] shifter_1_out;

  // Probe on in_1
  // Probe on in_2
  Negator #(.width(6)) negator_1 (.in(in_1), .out(negator_1_out));
  Transistor #(.\type ("n"), .gate("br"), .width(6)) transistor_1 (
    .in(negator_1_out), .out(transistor_1_out), .gate(counter_2_q));
  Transistor #(.width(6)) transistor_2 (.in(in_1), .out(transistor_1_out), .gate(counter_2_q));
  Transistor #(.\type ("n"), .gate("br"), .width(6)) transistor_3 (
    .in(negator_2_out), .out(transistor_3_out), .gate(counter_1_q));
  Negator #(.width(6)) negator_2 (.in(in_2), .out(negator_2_out));
  Transistor #(.width(6)) transistor_4 (.in(in_2), .out(transistor_3_out), .gate(counter_1_q));
  Counter #(.width(1), .max('h1)) counter_1 (.Q(counter_1_q), .clk(or_1_out));  // open: load, D, count, carry, clr
  or or_1 (or_1_out, and_2_out, nor_1_out);
  nor nor_1 (nor_1_out, bit_extender_2_out[0], bit_extender_2_out[1], bit_extender_2_out[2], bit_extender_2_out[3], bit_extender_2_out[4]);
  Counter #(.width(1), .max('h1)) counter_2 (.Q(counter_2_q), .clk(or_2_out));  // open: load, D, count, carry, clr
  and and_1 (and_1_out, bit_extender_1_out[0], bit_extender_1_out[1], bit_extender_1_out[2], bit_extender_1_out[3], bit_extender_1_out[4]);
  or or_2 (or_2_out, and_1_out, nor_2_out);
  nor nor_2 (nor_2_out, bit_extender_1_out[0], bit_extender_1_out[1], bit_extender_1_out[2], bit_extender_1_out[3], bit_extender_1_out[4]);
  Register #(.width(6)) xv (.D(transistor_1_out), .Q(xv_q), .clk(clock_1_out));  // open: en, clr
  Clock clock_1 (.out(clock_1_out));
  Register #(.width(6)) yv (.D(transistor_3_out), .Q(yv_q), .clk(clock_2_out));  // open: en, clr
  Clock clock_2 (.out(clock_2_out));
  and and_2 (and_2_out, bit_extender_2_out[0], bit_extender_2_out[1], bit_extender_2_out[2], bit_extender_2_out[3], bit_extender_2_out[4]);
  Adder #(.width(6)) adder_1 (.a(xv_q), .b(x_q), .out(adder_1_out));  // open: cin, cout
  Adder #(.width(6)) adder_2 (.a(yv_q), .b(y_q), .out(adder_2_out));  // open: cin, cout
  Register #(.width(6)) x (.D(adder_1_out), .Q(x_q), .clk(in_3));  // open: en, clr
  Register #(.width(6)) y (.D(adder_2_out), .Q(y_q), .clk(in_3));  // open: en, clr
  Bit_Extender #(.in_width(6), .out_width(5)) bit_extender_1 (.in(x_q), .out(bit_extender_1_out));
  Bit_Extender #(.in_width(6), .out_width(5)) bit_extender_2 (.in(y_q), .out(bit_extender_2_out));
  Shifter #(.width(32), .shift("lr")) shifter_1 (.in(32'h80000000), .\dist (bit_extender_1_out), .out(shifter_1_out));
  assign xnor_1_out = ~(bit_extender_2_out ^ in_4);  // XNOR_Gate xnor_1, 5 bits wide
  and and_3 (and_3_out, xnor_1_out[0], xnor_1_out[1], xnor_1_out[2], xnor_1_out[3], xnor_1_out[4]);
  Transistor #(.gate("br"), .width(32)) transistor_5 (.in({32{1'b0}}), .out(out_5), .gate(and_3_out));
  Transistor #(.\type ("n"), .width(32)) transistor_6 (.in(shifter_1_out), .out(out_5), .gate(and_3_out));
endmodule

module _32_buffer_extendable__4 (
  input  [31:0] in_1,
  input  w,
  input  block,
  input  [4:0] y,
  output [31:0] out_5,
  output [31:0] out_6,
  output [31:0] out_7,
  output [31:0] out_8,
  output [31:0] out_9,
  output [31:0] out_10,
  output [31:0] out_11,
  output [31:0] out_12,
  output [31:0] out_13,
  output [31:0] out_14,
  output [31:0] out_15,
  output [31:0] out_16,
  output [31:0] out_17,
  output [31:0] out_18,
  output [31:0] out_19,
  output [31:0] out_20,
  output [31:0] out_21,
  output [31:0] out_22,
  output [31:0] out_23,
  output [31:0] out_24,
  output [31:0] out_25,
  output [31:0] out_26,
  output [31:0] out_27,
  output [31:0] out_28,
  output [31:0] out_29,
  output [31:0] out_30,
  output [31:0] out_31,
  output [31:0] out_32,
  output [31:0] out_33,
  output [31:0] out_34,
  output [31:0] out_35,
  output [31:0] out_36
);

  wire _0, _1, _2, _3, _4, _5, _6, _7, _8, _9, _10, _11, _12, _13, _14, _15, _16, _17, _18, _19, _20, _21,
       _22, _23, _24, _25, _26, _27, _28, _29, _30, _31, clock_1_out, nor_1_out;

  Demultiplexer #(.select(5), .disabled(0)) demultiplexer_1 (
    .out0(_0), .out1(_1), .out2(_2), .out3(_3), .out4(_4), .out5(_5), .out6(_6), .out7(_7), .out8(_8),
    .out9(_9), .out10(_10), .out11(_11), .out12(_12), .out13(_13), .out14(_14), .out15(_15), .out16(_16),
    .out17(_17), .out18(_18), .out19(_19), .out20(_20), .out21(_21), .out22(_22), .out23(_23), .out24(_24),
    .out25(_25), .out26(_26), .out27(_27), .out28(_28), .out29(_29), .out30(_30), .out31(_31), .in(1'b1),
    .sel(y), .en(nor_1_out));
  nor nor_1 (nor_1_out, block, clock_1_out);
  Clock clock_1 (.out(clock_1_out));
  _32buffer_el u_32buffer_el_1 (.\input (in_1), ._1___buffer_read(_0), .video(out_5), ._1___buffer_write___clr(w));
  _32buffer_el u_32buffer_el_2 (.\input (in_1), ._1___buffer_read(_1), .video(out_6), ._1___buffer_write___clr(w));
  _32buffer_el u_32buffer_el_3 (.\input (in_1), ._1___buffer_read(_2), .video(out_7), ._1___buffer_write___clr(w));
  _32buffer_el u_32buffer_el_4 (.\input (in_1), ._1___buffer_read(_3), .video(out_8), ._1___buffer_write___clr(w));
  _32buffer_el u_32buffer_el_5 (.\input (in_1), ._1___buffer_read(_4), .video(out_9), ._1___buffer_write___clr(w));
  _32buffer_el u_32buffer_el_6 (.\input (in_1), ._1___buffer_read(_5), .video(out_10), ._1___buffer_write___clr(w));
  _32buffer_el u_32buffer_el_7 (.\input (in_1), ._1___buffer_read(_6), .video(out_11), ._1___buffer_write___clr(w));
  _32buffer_el u_32buffer_el_8 (.\input (in_1), ._1___buffer_read(_7), .video(out_12), ._1___buffer_write___clr(w));
  _32buffer_el u_32buffer_el_9 (.\input (in_1), ._1___buffer_read(_8), .video(out_13), ._1___buffer_write___clr(w));
  _32buffer_el u_32buffer_el_10 (.\input (in_1), ._1___buffer_read(_9), .video(out_14), ._1___buffer_write___clr(w));
  _32buffer_el u_32buffer_el_11 (.\input (in_1), ._1___buffer_read(_10), .video(out_15), ._1___buffer_write___clr(w));
  _32buffer_el u_32buffer_el_12 (.\input (in_1), ._1___buffer_read(_11), .video(out_16), ._1___buffer_write___clr(w));
  _32buffer_el u_32buffer_el_13 (.\input (in_1), ._1___buffer_read(_12), .video(out_17), ._1___buffer_write___clr(w));
  _32buffer_el u_32buffer_el_14 (.\input (in_1), ._1___buffer_read(_13), .video(out_18), ._1___buffer_write___clr(w));
  _32buffer_el u_32buffer_el_15 (.\input (in_1), ._1___buffer_read(_14), .video(out_19), ._1___buffer_write___clr(w));
  _32buffer_el u_32buffer_el_16 (.\input (in_1), ._1___buffer_read(_15), .video(out_20), ._1___buffer_write___clr(w));
  _32buffer_el u_32buffer_el_17 (.\input (in_1), ._1___buffer_read(_16), .video(out_21), ._1___buffer_write___clr(w));
  _32buffer_el u_32buffer_el_18 (.\input (in_1), ._1___buffer_read(_17), .video(out_22), ._1___buffer_write___clr(w));
  _32buffer_el u_32buffer_el_19 (.\input (in_1), ._1___buffer_read(_18), .video(out_23), ._1___buffer_write___clr(w));
  _32buffer_el u_32buffer_el_20 (.\input (in_1), ._1___buffer_read(_19), .video(out_24), ._1___buffer_write___clr(w));
  _32buffer_el u_32buffer_el_21 (.\input (in_1), ._1___buffer_read(_20), .video(out_25), ._1___buffer_write___clr(w));
  _32buffer_el u_32buffer_el_22 (.\input (in_1), ._1___buffer_read(_21), .video(out_26), ._1___buffer_write___clr(w));
  _32buffer_el u_32buffer_el_23 (.\input (in_1), ._1___buffer_read(_22), .video(out_27), ._1___buffer_write___clr(w));
  _32buffer_el u_32buffer_el_24 (.\input (in_1), ._1___buffer_read(_23), .video(out_28), ._1___buffer_write___clr(w));
  _32buffer_el u_32buffer_el_25 (.\input (in_1), ._1___buffer_read(_24), .video(out_29), ._1___buffer_write___clr(w));
  _32buffer_el u_32buffer_el_26 (.\input (in_1), ._1___buffer_read(_25), .video(out_30), ._1___buffer_write___clr(w));
  _32buffer_el u_32buffer_el_27 (.\input (in_1), ._1___buffer_read(_26), .video(out_31), ._1___buffer_write___clr(w));
  _32buffer_el u_32buffer_el_28 (.\input (in_1), ._1___buffer_read(_27), .video(out_32), ._1___buffer_write___clr(w));
  _32buffer_el u_32buffer_el_29 (.\input (in_1), ._1___buffer_read(_28), .video(out_33), ._1___buffer_write___clr(w));
  _32buffer_el u_32buffer_el_30 (.\input (in_1), ._1___buffer_read(_29), .video(out_34), ._1___buffer_write___clr(w));
  _32buffer_el u_32buffer_el_31 (.\input (in_1), ._1___buffer_read(_30), .video(out_35), ._1___buffer_write___clr(w));
  _32buffer_el u_32buffer_el_32 (.\input (in_1), ._1___buffer_read(_31), .video(out_36), ._1___buffer_write___clr(w));

  // Other names for the same wires on the sheet: inp[31:0] = in_1

  // Notes on the sheet:
  //   block: pull=down
endmodule

module _64x64_ball (
  input  [6:0] vx,
  input  [6:0] vy,
  input  in_3,
  input  [5:0] cur_row,
  output [6:0] debug_x,
  output [6:0] debug_y,
  output [31:0] line_x1,
  output [31:0] line_x2
);

  wire and_1_out, and_2_out, and_3_out, and_4_out, and_5_out, clock_1_out, clock_2_out, counter_1_q,
       counter_2_q, nor_1_out, nor_2_out, not_1_out, not_2_out, or_1_out, or_2_out;
  wire [4:0] demultiplexer_1_out0, demultiplexer_1_out1;
  wire [5:0] bit_extender_1_out, bit_extender_2_out, xnor_1_out;
  wire [6:0] adder_1_out, adder_2_out, negator_1_out, negator_2_out, transistor_1_out, transistor_3_out,
       xv_q, yv_q;
  wire [31:0] shifter_1_out, shifter_2_out;

  // Probe on vx
  // Probe on vy
  Negator #(.width(7)) negator_1 (.in(vx), .out(negator_1_out));
  Transistor #(.\type ("n"), .gate("br"), .width(7)) transistor_1 (
    .in(negator_1_out), .out(transistor_1_out), .gate(counter_2_q));
  Transistor #(.width(7)) transistor_2 (.in(vx), .out(transistor_1_out), .gate(counter_2_q));
  Negator #(.width(7)) negator_2 (.in(vy), .out(negator_2_out));
  Transistor #(.\type ("n"), .gate("br"), .width(7)) transistor_3 (
    .in(negator_2_out), .out(transistor_3_out), .gate(counter_1_q));
  Transistor #(.width(7)) transistor_4 (.in(vy), .out(transistor_3_out), .gate(counter_1_q));
  Counter #(.width(1), .max('h1)) counter_1 (.Q(counter_1_q), .clk(or_1_out));  // open: load, D, count, carry, clr
  and and_1 (and_1_out, bit_extender_2_out[0], bit_extender_2_out[1], bit_extender_2_out[2], bit_extender_2_out[3], bit_extender_2_out[4], bit_extender_2_out[5]);
  or or_1 (or_1_out, and_1_out, nor_1_out);
  nor nor_1 (nor_1_out, bit_extender_2_out[0], bit_extender_2_out[1], bit_extender_2_out[2], bit_extender_2_out[3], bit_extender_2_out[4], bit_extender_2_out[5]);
  Counter #(.width(1), .max('h1)) counter_2 (.Q(counter_2_q), .clk(or_2_out));  // open: load, D, count, carry, clr
  and and_2 (and_2_out, bit_extender_1_out[0], bit_extender_1_out[1], bit_extender_1_out[2], bit_extender_1_out[3], bit_extender_1_out[4], bit_extender_1_out[5]);
  or or_2 (or_2_out, and_2_out, nor_2_out);
  nor nor_2 (nor_2_out, bit_extender_1_out[0], bit_extender_1_out[1], bit_extender_1_out[2], bit_extender_1_out[3], bit_extender_1_out[4], bit_extender_1_out[5]);
  Register #(.width(7)) xv (.D(transistor_1_out), .Q(xv_q), .clk(clock_1_out));  // open: en, clr
  Clock clock_1 (.out(clock_1_out));
  Register #(.width(7)) yv (.D(transistor_3_out), .Q(yv_q), .clk(clock_2_out));  // open: en, clr
  Clock clock_2 (.out(clock_2_out));
  Adder #(.width(7)) adder_1 (.a(xv_q), .b(debug_x), .out(adder_1_out));  // open: cin, cout
  Adder #(.width(7)) adder_2 (.a(yv_q), .b(debug_y), .out(adder_2_out));  // open: cin, cout
  Register #(.width(7)) x (.D(adder_1_out), .Q(debug_x), .clk(in_3));  // open: en, clr
  Register #(.width(7)) y (.D(adder_2_out), .Q(debug_y), .clk(in_3));  // open: en, clr
  // Probe on cur_row
  Demultiplexer #(.width(5), .enable("false")) demultiplexer_1 (
    .out0(demultiplexer_1_out0), .out1(demultiplexer_1_out1), .in(bit_extender_1_out[4:0]), .sel(not_1_out));
  not not_1 (not_1_out, bit_extender_1_out[5]);
  Bit_Extender #(.in_width(7), .out_width(6)) bit_extender_1 (.in(debug_x), .out(bit_extender_1_out));
  // Probe on bit_extender_2_out
  Bit_Extender #(.in_width(7), .out_width(6)) bit_extender_2 (.in(debug_y), .out(bit_extender_2_out));
  assign xnor_1_out = ~(bit_extender_2_out ^ cur_row);  // XNOR_Gate xnor_1, 6 bits wide
  Shifter #(.width(32), .shift("lr")) shifter_1 (.in(32'h80000000), .\dist (demultiplexer_1_out1), .out(shifter_1_out));
  not not_2 (not_2_out, bit_extender_1_out[5]);
  and and_3 (and_3_out, xnor_1_out[0], xnor_1_out[1], xnor_1_out[2], xnor_1_out[3], xnor_1_out[4], xnor_1_out[5]);
  and and_4 (and_4_out, and_3_out, not_2_out);
  Transistor #(.\type ("n"), .width(32)) transistor_5 (.in(shifter_1_out), .out(line_x1), .gate(and_4_out));
  Transistor #(.gate("br"), .width(32)) transistor_6 (.in({32{1'b0}}), .out(line_x1), .gate(and_4_out));
  and and_5 (and_5_out, bit_extender_1_out[5], and_3_out);
  Shifter #(.width(32), .shift("lr")) shifter_2 (.in(32'h80000000), .\dist (demultiplexer_1_out0), .out(shifter_2_out));
  Transistor #(.\type ("n"), .width(32)) transistor_7 (.in(shifter_2_out), .out(line_x2), .gate(and_5_out));
  Transistor #(.gate("br"), .width(32)) transistor_8 (.in({32{1'b0}}), .out(line_x2), .gate(and_5_out));
endmodule

module obj_module (
  input  [6:0] vx,
  input  [6:0] vy,
  input  update,
  input  [5:0] cur_line,
  output [31:0] line_x1,
  output [31:0] line_x2
);

  wire and_1_out, and_2_out, and_3_out, clock_1_out, clock_2_out, comparator_1_eq, comparator_1_gt,
       comparator_2_lt, comparator_3_lt, comparator_4_eq, comparator_4_gt, comparator_5_lt, comparator_6_eq,
       counter_1_q, counter_2_q, not_1_out, not_2_out, not_3_out, or_1_out, or_2_out, or_3_out, or_4_out,
       subtractor_2_bout, subtractor_3_bout;
  wire [4:0] bit_extender_3_out, bit_extender_4_out, multiplexer_1_out, multiplexer_2_out, multiplexer_4_out,
       subtractor_3_out, subtractor_4_out;
  wire [5:0] bit_extender_1_out, bit_extender_2_out, subtractor_1_out, subtractor_2_out;
  wire [6:0] adder_1_out, adder_2_out, negator_1_out, negator_2_out, transistor_1_out, transistor_3_out, x_q,
       xv_q, y_q, yv_q;
  wire [31:0] n32_bit_reverse_1_out_2, rom_1_data, shifter_1_out, shifter_2_out, shifter_3_out;

  // Probe on vx
  // Probe on vy
  Counter #(.width(1), .max('h1)) counter_1 (.Q(counter_1_q), .clk(or_1_out));  // open: load, D, count, carry, clr
  or or_1 (or_1_out, comparator_3_lt, or_3_out);
  Negator #(.width(7)) negator_1 (.in(vx), .out(negator_1_out));
  Transistor #(.\type ("n"), .gate("br"), .width(7)) transistor_1 (
    .in(negator_1_out), .out(transistor_1_out), .gate(counter_1_q));
  Transistor #(.width(7)) transistor_2 (.in(vx), .out(transistor_1_out), .gate(counter_1_q));
  Negator #(.width(7)) negator_2 (.in(vy), .out(negator_2_out));
  Counter #(.width(1), .max('h1)) counter_2 (.Q(counter_2_q), .clk(or_2_out));  // open: load, D, count, carry, clr
  or or_2 (or_2_out, or_4_out, comparator_2_lt);
  Register #(.width(7)) xv (.D(transistor_1_out), .Q(xv_q), .clk(clock_1_out));  // open: en, clr
  Clock clock_1 (.out(clock_1_out));
  Transistor #(.\type ("n"), .gate("br"), .width(7)) transistor_3 (
    .in(negator_2_out), .out(transistor_3_out), .gate(counter_2_q));
  Register #(.width(7)) yv (.D(transistor_3_out), .Q(yv_q), .clk(clock_2_out));  // open: en, clr
  Transistor #(.width(7)) transistor_4 (.in(vy), .out(transistor_3_out), .gate(counter_2_q));
  Clock clock_2 (.out(clock_2_out));
  Comparator #(.width(7)) comparator_1 (
    .a({7{1'b0}}), .b(y_q), .gt(comparator_1_gt), .eq(comparator_1_eq));  // open: lt
  Comparator #(.width(7)) comparator_2 (.a(7'b0111100), .b(y_q), .lt(comparator_2_lt));  // open: gt, eq
  Comparator #(.width(7)) comparator_3 (.a(7'b0111100), .b(x_q), .lt(comparator_3_lt));  // open: gt, eq
  or or_3 (or_3_out, comparator_4_gt, comparator_4_eq);
  Comparator #(.width(7)) comparator_4 (
    .a({7{1'b0}}), .b(x_q), .gt(comparator_4_gt), .eq(comparator_4_eq));  // open: lt
  Adder #(.width(7)) adder_1 (.a(xv_q), .b(x_q), .out(adder_1_out));  // open: cin, cout
  Adder #(.width(7)) adder_2 (.a(yv_q), .b(y_q), .out(adder_2_out));  // open: cin, cout
  or or_4 (or_4_out, comparator_1_gt, comparator_1_eq);
  Register #(.width(7)) x (.D(adder_1_out), .Q(x_q), .clk(update));  // open: en, clr
  Register #(.width(7)) y (.D(adder_2_out), .Q(y_q), .clk(update));  // open: en, clr
  Bit_Extender #(.in_width(7), .out_width(6)) bit_extender_1 (.in(x_q), .out(bit_extender_1_out));
  Bit_Extender #(.in_width(7), .out_width(6)) bit_extender_2 (.in(y_q), .out(bit_extender_2_out));
  Subtractor #(.width(6)) subtractor_1 (
    .a(cur_line), .b(bit_extender_2_out), .out(subtractor_1_out));  // open: bin, bout
  Subtractor #(.width(6)) subtractor_2 (
    .a(cur_line), .b(bit_extender_2_out), .out(subtractor_2_out), .bout(subtractor_2_bout));  // open: bin
  // Probe on cur_line
  Bit_Extender #(.in_width(6), .out_width(5)) bit_extender_3 (.in(subtractor_1_out), .out(bit_extender_3_out));
  Comparator #(.width(6), .mode("unsigned")) comparator_5 (
    .a(subtractor_2_out), .b(6'b100000), .lt(comparator_5_lt));  // open: gt, eq
  // Probe on bit_extender_1_out[4:0]
  not not_1 (not_1_out, bit_extender_1_out[5]);
  Comparator #(.width(6), .mode("unsigned")) comparator_6 (
    .a(bit_extender_1_out), .b({6{1'b0}}), .eq(comparator_6_eq));  // open: gt, lt
  not not_2 (not_2_out, comparator_6_eq);
  and and_1 (and_1_out, comparator_5_lt, not_3_out);
  not not_3 (not_3_out, subtractor_2_bout);
  ROM #(.addrWidth(5), .dataWidth(32)) rom_1 (.addr(bit_extender_3_out), .data(rom_1_data));  // open: sel
  assign bit_extender_4_out = {{4{1'b0}}, not_1_out};  // Bit_Extender bit_extender_4
  _32_bit_reverse u_32_bit_reverse_1 (.in_1(rom_1_data), .out_2(n32_bit_reverse_1_out_2));
  Subtractor #(.width(5)) subtractor_3 (
    .a(bit_extender_1_out[4:0]), .b(bit_extender_4_out), .out(subtractor_3_out), .bout(subtractor_3_bout));  // open: bin
  Multiplexer #(.width(5), .enable("false")) multiplexer_1 (
    .in0(subtractor_3_out), .in1({5{1'b0}}), .out(multiplexer_1_out), .sel(subtractor_3_bout));
  // Probe on {5{1'b1}}
  // Probe on subtractor_4_out
  Subtractor #(.width(5)) subtractor_4 (
    .a({5{1'b1}}), .b(multiplexer_1_out), .out(subtractor_4_out));  // open: bin, bout
  Shifter #(.width(32), .shift("lr")) shifter_1 (
    .in(n32_bit_reverse_1_out_2), .\dist (bit_extender_1_out[4:0]), .out(shifter_1_out));
  and and_2 (and_2_out, not_1_out, and_1_out);
  Multiplexer #(.width(5), .enable("false")) multiplexer_2 (
    .in0({5{1'b0}}), .in1(subtractor_4_out), .out(multiplexer_2_out), .sel(not_1_out));
  Multiplexer #(.width(32), .enable("false")) multiplexer_3 (
    .in0({32{1'b0}}), .in1(shifter_1_out), .out(line_x1), .sel(and_2_out));
  Shifter #(.width(32)) shifter_2 (.in(n32_bit_reverse_1_out_2), .\dist (multiplexer_2_out), .out(shifter_2_out));
  Multiplexer #(.width(5), .enable("false")) multiplexer_4 (
    .in0(bit_extender_1_out[4:0]), .in1({5{1'b0}}), .out(multiplexer_4_out), .sel(not_1_out));
  Shifter #(.width(32), .shift("lr")) shifter_3 (.in(shifter_2_out), .\dist (multiplexer_4_out), .out(shifter_3_out));
  and and_3 (and_3_out, not_2_out, and_1_out);
  Multiplexer #(.width(32), .enable("false")) multiplexer_5 (
    .in0({32{1'b0}}), .in1(shifter_3_out), .out(line_x2), .sel(and_3_out));

  // Notes on the sheet:
  //   address = y-line
  //   0 <= y-line < 32
  //   contents of rom_1 (hex, n*v repeats v):
  //   5 2 5
  //   +1 for shift left line x2
  //   to simulate shift by 32
  //   idk i just like that
  //   smth will work on line x2
  //   only if shift right > 0
  //   (still for simulate 32 shift)
  //   line x1 will work only if shift right < 32
  //   if x=0 shift left for line x2 must be 32 (with simulation of 32 shift)
  //   shift left for line x2
  //   shift rigth for line x2
  //   shift right works only if shift left = 0
endmodule

module _32_bit_reverse (
  input  [31:0] in_1,
  output [31:0] out_2
);


  assign out_2 = {in_1[0], in_1[1], in_1[2], in_1[3], in_1[4], in_1[5], in_1[6], in_1[7], in_1[8], in_1[9], in_1[10], in_1[11], in_1[12], in_1[13], in_1[14], in_1[15], in_1[16], in_1[17], in_1[18], in_1[19], in_1[20], in_1[21], in_1[22], in_1[23], in_1[24], in_1[25], in_1[26], in_1[27], in_1[28], in_1[29], in_1[30], in_1[31]};
endmodule

module abst_obj (
  input  write,
  input  [4:0] texture_line,
  input  [31:0] texture_input,
  input  [6:0] x,
  input  [6:0] y,
  input  draw,
  output [31:0] line_x1,
  output [31:0] line_x2,
  output [5:0] cur_line,
  output drawing
);

  wire and_1_out, and_2_out, and_3_out, comparator_1_lt, comparator_2_eq, counter_1_carry, drawing_q,
       not_1_out, not_2_out, not_4_out, not_5_out, not_6_out, register_1_q, subtractor_2_bout,
       subtractor_3_bout, transistor_3_out, x_upt, y_upd;
  wire [4:0] bit_extender_3_out, bit_extender_5_out, counter_1_q, multiplexer_1_out, multiplexer_2_out,
       multiplexer_4_out, subtractor_3_out, subtractor_4_out, transistor_1_out;
  wire [5:0] adder_1_out, bit_extender_1_out, bit_extender_2_out, bit_extender_4_out, subtractor_1_out,
       subtractor_2_out;
  wire [31:0] n32_bit_reverse_1_out_2, ram_1_data, shifter_1_out, shifter_2_out, shifter_3_out;

  // Probe on x
  // Probe on y
  Register #(.width(1)) register_1 (.D(draw), .Q(register_1_q), .clk(draw), .clr(counter_1_carry));  // open: en
  Register #(.width(1)) u_drawing (
    .D(register_1_q), .Q(drawing_q), .clk(not_1_out), .clr(counter_1_carry));  // open: en
  not not_1 (not_1_out, y_upd);
  or or_1 (drawing, register_1_q, drawing_q);
  Bit_Extender #(.in_width(7), .out_width(6)) bit_extender_1 (.in(x), .out(bit_extender_1_out));
  Bit_Extender #(.in_width(7), .out_width(6)) bit_extender_2 (.in(y), .out(bit_extender_2_out));
  // Probe on adder_1_out
  Bit_Extender #(.in_width(6), .out_width(5)) bit_extender_3 (.in(subtractor_1_out), .out(bit_extender_3_out));
  Subtractor #(.width(6)) subtractor_1 (
    .a(adder_1_out), .b(bit_extender_2_out), .out(subtractor_1_out));  // open: bin, bout
  Counter #(.width(5), .max('h3)) counter_1 (
    .count(drawing_q), .Q(counter_1_q), .carry(counter_1_carry), .clk(x_upt), .clr(counter_1_carry));  // open: load, D
  Subtractor #(.width(6)) subtractor_2 (
    .a(adder_1_out), .b(bit_extender_2_out), .out(subtractor_2_out), .bout(subtractor_2_bout));  // open: bin
  not not_2 (not_2_out, drawing_q);
  Register #(.width(6)) register_2 (.D(adder_1_out), .Q(cur_line), .clk(y_upd), .clr(not_2_out));  // open: en
  Transistor #(.gate("br"), .width(5)) transistor_1 (.in(texture_line), .out(transistor_1_out), .gate(register_1_q));
  Transistor #(.\type ("n"), .width(5)) transistor_2 (
    .in(bit_extender_3_out), .out(transistor_1_out), .gate(register_1_q));
  assign bit_extender_4_out = {{1{1'b0}}, counter_1_q};  // Bit_Extender bit_extender_4
  Comparator #(.width(6), .mode("unsigned")) comparator_1 (
    .a(subtractor_2_out), .b(6'b100000), .lt(comparator_1_lt));  // open: gt, eq
  not not_3 (x_upt, y_upd);
  Transistor #(.gate("br")) transistor_3 (.in(write), .out(transistor_3_out), .gate(register_1_q));
  // Probe on bit_extender_1_out[4:0]
  not not_4 (not_4_out, bit_extender_1_out[5]);
  Adder #(.width(6)) adder_1 (.a(bit_extender_2_out), .b(bit_extender_4_out), .out(adder_1_out));  // open: cin, cout
  not not_5 (not_5_out, comparator_2_eq);
  Comparator #(.width(6), .mode("unsigned")) comparator_2 (
    .a(bit_extender_1_out), .b({6{1'b0}}), .eq(comparator_2_eq));  // open: gt, lt
  and and_1 (and_1_out, comparator_1_lt, not_6_out);
  not not_6 (not_6_out, subtractor_2_bout);
  Clock clock_1 (.out(y_upd));
  assign bit_extender_5_out = {{4{1'b0}}, not_4_out};  // Bit_Extender bit_extender_5
  _32_bit_reverse u_32_bit_reverse_1 (.in_1(ram_1_data), .out_2(n32_bit_reverse_1_out_2));
  RAM #(.addrWidth(5), .dataWidth(32), .bus("separate")) ram_1 (
    .addr(transistor_1_out), .din(texture_input), .data(ram_1_data), .clk(transistor_3_out));  // open: str, sel, ld, clr
  Subtractor #(.width(5)) subtractor_3 (
    .a(bit_extender_1_out[4:0]), .b(bit_extender_5_out), .out(subtractor_3_out), .bout(subtractor_3_bout));  // open: bin
  Multiplexer #(.width(5), .enable("false")) multiplexer_1 (
    .in0(subtractor_3_out), .in1({5{1'b0}}), .out(multiplexer_1_out), .sel(subtractor_3_bout));
  // Probe on {5{1'b1}}
  // Probe on subtractor_4_out
  Subtractor #(.width(5)) subtractor_4 (
    .a({5{1'b1}}), .b(multiplexer_1_out), .out(subtractor_4_out));  // open: bin, bout
  Shifter #(.width(32), .shift("lr")) shifter_1 (
    .in(n32_bit_reverse_1_out_2), .\dist (bit_extender_1_out[4:0]), .out(shifter_1_out));
  Multiplexer #(.width(5), .enable("false")) multiplexer_2 (
    .in0({5{1'b0}}), .in1(subtractor_4_out), .out(multiplexer_2_out), .sel(not_4_out));
  and and_2 (and_2_out, not_4_out, register_1_q, drawing_q, and_1_out);
  Multiplexer #(.width(32), .enable("false")) multiplexer_3 (
    .in0({32{1'b0}}), .in1(shifter_1_out), .out(line_x1), .sel(and_2_out));
  Shifter #(.width(32)) shifter_2 (.in(n32_bit_reverse_1_out_2), .\dist (multiplexer_2_out), .out(shifter_2_out));
  Multiplexer #(.width(5), .enable("false")) multiplexer_4 (
    .in0(bit_extender_1_out[4:0]), .in1({5{1'b0}}), .out(multiplexer_4_out), .sel(not_4_out));
  Shifter #(.width(32), .shift("lr")) shifter_3 (.in(shifter_2_out), .\dist (multiplexer_4_out), .out(shifter_3_out));
  and and_3 (and_3_out, not_5_out, register_1_q, and_1_out, drawing_q);
  Multiplexer #(.width(32), .enable("false")) multiplexer_5 (
    .in0({32{1'b0}}), .in1(shifter_3_out), .out(line_x2), .sel(and_3_out));

  // Notes on the sheet:
  //   address = line-y
  //   0 <= y-line < 32
  //   +1 for shift left line x2
  //   to simulate shift by 32
  //   idk i just like that
  //   line x1 will work only if shift right < 32
  //   smth will work on line x2
  //   only if shift right > 0
  //   (still for simulate 32 shift)
  //   if x=0 shift left for line x2 must be 32 (with simulation of 32 shift)
  //   shift left for line x2
  //   shift rigth for line x2
  //   shift right works only if shift left = 0
endmodule

module player_multiobject (
  input  collide_check,
  input  [15:0] x,
  input  \wait ,
  input  [15:0] x_col,
  input  end_cycle,
  input  draw,
  input  clock,
  input  [15:0] y_col,
  output initing,
  output [15:0] collided,
  output [15:0] id,
  output [15:0] x_2,
  output [15:0] y,
  output [15:0] command,
  output ready
);

  wire and_1_out, and_2_out, and_3_out, collided_t, comparator_1_gt, comparator_2_lt, comparator_3_eq,
       comparator_4_eq, comparator_5_lt, comparator_6_eq, comparator_6_gt, comparator_7_gt, counter_1_carry,
       d_ff_1_q, draw_t, init_step, nor_1_out, not_2_out, not_3_out, not_4_out, not_5_out, not_6_out,
       not_7_out, or_1_out, or_2_out, register_1_q, register_2_q, transistor_1_out;
  wire [1:0] counter_1_q;
  wire [2:0] counter_2_q;
  wire [15:0] adder_1_out, controlled_buffer_1_out, controlled_buffer_2_out, controlled_buffer_3_out,
       controlled_buffer_4_out, divider_1_out, divider_2_out, multiplexer_1_out, multiplexer_3_out,
       multiplexer_4_out, multiplexer_5_out, subtractor_1_out, subtractor_2_out, x_t;

  Counter #(.width(2), .max('h2)) counter_1 (
    .Q(counter_1_q), .carry(counter_1_carry), .clk(clock), .clr(register_1_q));  // open: load, D, count
  Bit_Extender #(.in_width(2), .out_width(1)) bit_extender_1 (.in(counter_1_q), .out(init_step));
  or or_1 (or_1_out, end_cycle, ready);
  not not_1 (initing, register_1_q);
  Register #(.width(1)) register_1 (.D(counter_1_carry), .Q(register_1_q), .clk(counter_1_carry));  // open: en, clr
  Multiplexer #(.width(16), .enable("false")) multiplexer_1 (
    .in0(x), .in1(16'ha), .out(multiplexer_1_out), .sel(initing));
  not not_2 (not_2_out, \wait );
  Register #(.width(1)) register_2 (.D(draw), .Q(register_2_q), .clk(draw), .clr(or_1_out));  // open: en
  Adder #(.width(16)) adder_1 (.a(x_t), .b(multiplexer_1_out), .out(adder_1_out));  // open: cin, cout
  Counter #(.width(3), .max('h3)) counter_2 (
    .Q(counter_2_q), .carry(ready), .clk(transistor_1_out), .clr(ready));  // open: load, D, count
  Transistor #(.\type ("n")) transistor_1 (.in(clock), .out(transistor_1_out), .gate(and_1_out));
  and and_1 (and_1_out, not_2_out, register_2_q);
  Multiplexer #(.enable("false")) multiplexer_2 (.in0(register_2_q), .in1(init_step), .out(draw_t), .sel(initing));
  Comparator #(.width(16), .mode("unsigned")) comparator_1 (
    .a(adder_1_out), .b(16'h3b), .gt(comparator_1_gt));  // open: eq, lt
  Comparator #(.width(16), .mode("unsigned")) comparator_2 (
    .a(adder_1_out), .b({16{1'b0}}), .lt(comparator_2_lt));  // open: gt, eq
  not not_3 (not_3_out, collided_t);
  nor nor_1 (nor_1_out, comparator_1_gt, comparator_2_lt);
  Comparator #(.width(3), .mode("unsigned")) comparator_3 (
    .a(counter_2_q), .b(3'b001), .eq(comparator_3_eq));  // open: gt, lt
  Comparator #(.width(3), .mode("unsigned")) comparator_4 (
    .a(counter_2_q), .b(3'b010), .eq(comparator_4_eq));  // open: gt, lt
  Transistor #(.\type ("n"), .width(16)) transistor_2 (.in(16'h1), .out(collided), .gate(d_ff_1_q));
  D_Flip_Flop #(.trigger("falling")) d_ff_1 (
    .clk(clock), .D(collided_t), .Q(d_ff_1_q), .reset(not_3_out));  // open: Qn, preset, en
  Multiplexer #(.width(16), .enable("false")) multiplexer_3 (
    .in0(x_t), .in1(adder_1_out), .out(multiplexer_3_out), .sel(nor_1_out));
  Register #(.width(16)) u_x (.D(multiplexer_3_out), .Q(x_t), .clk(draw_t));  // open: en, clr
  Multiplexer #(.width(16), .enable("false")) multiplexer_4 (
    .in0({16{1'b0}}), .in1(16'h1), .out(multiplexer_4_out), .sel(comparator_3_eq));
  assign controlled_buffer_1_out = draw_t ? {16{1'b0}} : 16'bz;  // Controlled_Buffer controlled_buffer_1
  not not_4 (not_4_out, initing);
  assign controlled_buffer_2_out = draw_t ? x_t : 16'bz;  // Controlled_Buffer controlled_buffer_2
  not not_5 (not_5_out, initing);
  assign controlled_buffer_3_out = draw_t ? 16'h38 : 16'bz;  // Controlled_Buffer controlled_buffer_3
  not not_6 (not_6_out, initing);
  Multiplexer #(.width(16), .enable("false")) multiplexer_5 (
    .in0(multiplexer_4_out), .in1(16'h2), .out(multiplexer_5_out), .sel(comparator_4_eq));
  assign controlled_buffer_4_out = draw_t ? multiplexer_5_out : 16'bz;  // Controlled_Buffer controlled_buffer_4
  not not_7 (not_7_out, initing);
  assign id = not_4_out ? controlled_buffer_1_out : 16'bz;  // Controlled_Buffer controlled_buffer_5
  assign x_2 = not_5_out ? controlled_buffer_2_out : 16'bz;  // Controlled_Buffer controlled_buffer_6
  assign y = not_6_out ? controlled_buffer_3_out : 16'bz;  // Controlled_Buffer controlled_buffer_7
  assign command = not_7_out ? controlled_buffer_4_out : 16'bz;  // Controlled_Buffer controlled_buffer_8
  Pull_Resistor pull_resistor_1 (.node(x_col));
  Pull_Resistor pull_resistor_2 (.node(y_col));
  // Probe on x_col
  Divider #(.width(16)) divider_1 (.a(x_t), .b(16'h2), .out(divider_1_out));  // open: upper, rem
  // Probe on y_col
  Divider #(.width(16)) divider_2 (.a(16'h38), .b(16'h2), .out(divider_2_out));  // open: upper, rem
  Subtractor #(.width(16)) subtractor_1 (.a(x_col), .b(divider_1_out), .out(subtractor_1_out));  // open: bin, bout
  // Probe on subtractor_2_out
  Subtractor #(.width(16)) subtractor_2 (.a(y_col), .b(divider_2_out), .out(subtractor_2_out));  // open: bin, bout
  // Probe on 16'hfffd
  Comparator #(.width(16)) comparator_5 (.a(subtractor_1_out), .b(16'h3), .lt(comparator_5_lt));  // open: gt, eq
  Comparator #(.width(16)) comparator_6 (
    .a(subtractor_1_out), .b({16{1'b0}}), .gt(comparator_6_gt), .eq(comparator_6_eq));  // open: lt
  Comparator #(.width(16)) comparator_7 (.a(subtractor_2_out), .b(16'hfffd), .gt(comparator_7_gt));  // open: eq, lt
  and and_2 (and_2_out, comparator_5_lt, or_2_out);
  or or_2 (or_2_out, comparator_6_gt, comparator_6_eq);
  and and_3 (and_3_out, and_2_out, comparator_7_gt);
  and and_4 (collided_t, and_3_out, collide_check);

  // Other names for the same wires on the sheet: clk = clock
endmodule

module enemies_multiobject (
  input  collide_check,
  input  \wait ,
  input  end_cycle,
  input  draw,
  input  [15:0] x_col,
  input  clock,
  input  [15:0] y_col,
  output [15:0] collided,
  output [15:0] id,
  output initing,
  output [15:0] y,
  output [4:0] DEBUG__enemy_cout,
  output [15:0] x,
  output [15:0] command,
  output [5:0] proc_command,
  output ready,
  output [15:0] speed
);

  wire alive, and_1_out, and_2_out, and_3_out, and_5_out, and_6_out, and_7_out, and_8_out, and_9_out,
       and_10_out, and_11_out, and_12_out, collided_t, comparator_1_eq, comparator_1_gt, comparator_2_eq,
       comparator_2_lt, comparator_3_lt, comparator_5_eq, comparator_5_lt, comparator_6_eq, comparator_6_lt,
       comparator_8_eq, comparator_8_lt, counter_1_carry, draw_t, may_collide, multiplexer_1_out, not_1_out,
       not_2_out, not_4_out, not_5_out, not_6_out, not_7_out, or_1_out, or_2_out, or_4_out, or_5_out,
       or_6_out, or_7_out, or_8_out, or_9_out, or_10_out, or_11_out, or_12_out, pull_resistor_1_node,
       pull_resistor_3_node, register_1_q, register_3_q, register_4_q, register_5_q, register_8_q,
       register_9_q, texture_state, transistor_3_out, wait_t, x_aligned, xnor_1_out;
  wire [4:0] col_adr, counter_1_q;
  wire [15:0] adder_1_out, adder_2_out, adder_3_out, adder_4_out, adder_5_out, adder_6_out, adder_7_out,
       adder_8_out, bit_extender_1_out, controlled_buffer_1_out, divider_1_out, divider_1_rem, divider_2_out,
       divider_3_out, divider_4_out, divider_4_rem, divider_5_out, divider_5_rem, multiplexer_4_out,
       multiplexer_5_out, multiplexer_6_out, multiplexer_7_out, multiplier_1_out, multiplier_2_out,
       multiplier_3_out, multiplier_4_out, multiplier_5_out, negator_1_out, negator_2_out, register_10_q,
       register_11_q, subtractor_1_out, subtractor_2_out, subtractor_3_out, x_t, y_t;

  or or_1 (or_1_out, end_cycle, ready);
  not not_1 (not_1_out, may_collide);
  Register #(.width(1)) register_1 (.D(or_2_out), .Q(register_1_q), .clk(clock));  // open: en, clr
  or or_2 (or_2_out, collide_check, \wait );
  Register #(.width(1)) register_2 (.D(register_3_q), .Q(draw_t), .clk(and_1_out), .clr(or_1_out));  // open: en
  Register #(.width(1)) register_3 (.D(draw), .Q(register_3_q), .clk(draw), .clr(or_1_out));  // open: en
  and and_1 (and_1_out, ~wait_t, clock);  // AND_Gate
  and and_2 (and_2_out, collided_t, alive);
  D_Flip_Flop #(.trigger("falling")) d_ff_1 (
    .clk(clock), .D(may_collide), .Q(collided_t), .reset(not_1_out));  // open: Qn, preset, en
  Counter #(.width(5), .max('he)) counter_1 (
    .Q(counter_1_q), .carry(counter_1_carry), .clk(not_2_out));  // open: load, D, count, clr
  or or_3 (wait_t, register_1_q, or_2_out);
  Transistor #(.\type ("n"), .width(16)) transistor_1 (.in(16'h2), .out(collided), .gate(and_2_out));
  not not_2 (not_2_out, multiplexer_1_out);
  Multiplexer #(.enable("false")) multiplexer_1 (
    .in0(clock), .in1(pull_resistor_1_node), .out(multiplexer_1_out), .sel(register_4_q));
  Pull_Resistor pull_resistor_1 (.node(pull_resistor_1_node));
  Transistor #(.\type ("n"), .gate("br")) transistor_2 (.in(or_4_out), .out(pull_resistor_1_node), .gate(draw_t));
  or or_4 (or_4_out, wait_t, and_3_out);
  not not_3 (initing, register_4_q);
  Multiplexer #(.width(5), .enable("false")) multiplexer_2 (
    .in0(counter_1_q), .in1(col_adr), .out(DEBUG__enemy_cout), .sel(may_collide));
  not not_4 (not_4_out, counter_1_carry);
  Register #(.width(1)) register_4 (.D(not_4_out), .Q(register_4_q), .clk(not_4_out));  // open: en, clr
  and and_3 (and_3_out, ~clock, ~and_5_out);  // AND_Gate
  Multiplexer #(.width(16), .enable("false")) multiplexer_3 (
    .in0(multiplexer_4_out), .in1({16{1'b0}}), .out(speed), .sel(initing));
  Transistor #(.gate("br")) transistor_3 (.in(1'b1), .out(transistor_3_out), .gate(register_4_q));
  Pull_Resistor pull_resistor_2 (.node(transistor_3_out));
  Negator #(.width(16)) negator_1 (.in(16'h1), .out(negator_1_out));
  assign bit_extender_1_out = {{11{1'b0}}, DEBUG__enemy_cout};  // Bit_Extender bit_extender_1
  xnor xnor_1 (xnor_1_out, collided_t, register_4_q);
  Register #(.width(1)) register_5 (.D(not_4_out), .Q(register_5_q), .clk(not_4_out), .clr(register_5_q));  // open: en
  // Probe on subtractor_3_out
  Adder #(.width(16)) adder_1 (.a(x_t), .b(multiplexer_4_out), .out(adder_1_out));  // open: cin, cout
  Multiplexer #(.width(16), .enable("false")) multiplexer_4 (
    .in0(16'h1), .in1(negator_1_out), .out(multiplexer_4_out), .sel(register_8_q));
  Adder #(.width(16)) adder_2 (.a(16'h2), .b(y_t), .out(adder_2_out));  // open: cin, cout
  RAM #(.addrWidth(5), .dataWidth(1), .bus("separate")) ram_1 (
    .addr(DEBUG__enemy_cout), .din(transistor_3_out), .data(alive), .str(xnor_1_out), .clk(clock));  // open: sel, ld, clr
  and and_4 (ready, register_5_q, draw_t);
  Register #(.width(16)) register_6 (.D(adder_1_out), .Q(x_t), .clk(draw_t));  // open: en, clr
  Register #(.width(16)) register_7 (.D(adder_2_out), .Q(y_t), .clk(and_6_out));  // open: en, clr
  Divider #(.width(16)) divider_1 (
    .a(bit_extender_1_out), .b(16'h5), .out(divider_1_out), .rem(divider_1_rem));  // open: upper
  and and_5 (and_5_out, alive, register_4_q);
  Comparator #(.width(16), .mode("unsigned")) comparator_1 (
    .a(x_t), .b(subtractor_3_out), .gt(comparator_1_gt), .eq(comparator_1_eq));  // open: lt
  and and_6 (and_6_out, register_9_q, ready);
  and and_7 (and_7_out, and_5_out, or_6_out);
  not not_5 (not_5_out, clock);
  Counter #(.width(1), .max('h1)) counter_2 (
    .Q(texture_state), .clk(register_5_q));  // open: load, D, count, carry, clr
  // Probe on negator_2_out
  or or_5 (or_5_out, comparator_1_gt, comparator_1_eq);
  Adder #(.width(16)) adder_3 (.a(16'h3), .b(divider_1_out), .out(adder_3_out));  // open: cin, cout
  Adder #(.width(16)) adder_4 (.a(16'h6), .b(divider_1_out), .out(adder_4_out));  // open: cin, cout
  Multiplier #(.width(16)) multiplier_1 (.a(divider_1_out), .b(16'ha), .out(multiplier_1_out));  // open: cin, cout
  Multiplier #(.width(16)) multiplier_2 (.a(divider_1_rem), .b(16'ha), .out(multiplier_2_out));  // open: cin, cout
  Multiplexer #(.width(16), .enable("false")) multiplexer_5 (
    .in0({16{1'b0}}), .in1(16'h1), .out(multiplexer_5_out), .sel(and_7_out));
  or or_6 (or_6_out, not_5_out, wait_t);
  Comparator #(.width(16)) comparator_2 (
    .a(x_t), .b(negator_2_out), .eq(comparator_2_eq), .lt(comparator_2_lt));  // open: gt
  or or_7 (or_7_out, comparator_2_eq, comparator_2_lt);
  or or_8 (or_8_out, or_5_out, and_8_out);
  Multiplexer #(.width(16), .enable("false")) multiplexer_6 (
    .in0(adder_3_out), .in1(adder_4_out), .out(multiplexer_6_out), .sel(texture_state));
  Adder #(.width(16)) adder_5 (.a(y_t), .b(multiplier_1_out), .out(adder_5_out));  // open: cin, cout
  Adder #(.width(16)) adder_6 (.a(x_t), .b(multiplier_2_out), .out(adder_6_out));  // open: cin, cout
  assign controlled_buffer_1_out = alive ? divider_1_rem : 16'bz;  // Controlled_Buffer controlled_buffer_1
  assign proc_command = draw_t ? 6'b000001 : 6'bz;  // Controlled_Buffer controlled_buffer_2
  Register #(.width(1)) register_8 (.D(or_5_out), .Q(register_8_q), .clk(or_5_out), .clr(and_8_out));  // open: en
  Register #(.width(1)) register_9 (.D(or_8_out), .Q(register_9_q), .clk(or_8_out), .clr(and_6_out));  // open: en
  assign id = draw_t ? multiplexer_6_out : 16'bz;  // Controlled_Buffer controlled_buffer_3
  assign y = draw_t ? adder_5_out : 16'bz;  // Controlled_Buffer controlled_buffer_4
  assign x = draw_t ? adder_6_out : 16'bz;  // Controlled_Buffer controlled_buffer_5
  assign command = draw_t ? multiplexer_5_out : 16'bz;  // Controlled_Buffer controlled_buffer_6
  and and_8 (and_8_out, or_7_out, register_8_q);
  Comparator #(.width(16), .mode("unsigned")) comparator_3 (
    .a(controlled_buffer_1_out), .b(register_11_q), .lt(comparator_3_lt));  // open: gt, eq
  Register #(.width(16)) register_10 (
    .D(controlled_buffer_1_out), .Q(register_10_q), .clk(and_9_out), .clr(not_6_out));  // open: en
  and and_9 (and_9_out, pull_resistor_3_node, wait_t);
  Pull_Resistor pull_resistor_3 (.node(pull_resistor_3_node));
  Comparator #(.width(16), .mode("unsigned")) comparator_4 (
    .a(controlled_buffer_1_out), .b(register_10_q), .gt(pull_resistor_3_node));  // open: eq, lt
  Pull_Resistor pull_resistor_4 (.node(x_col));
  Pull_Resistor pull_resistor_5 (.node(y_col));
  Multiplexer #(.width(16), .enable("false")) multiplexer_7 (
    .in0(16'h30), .in1(controlled_buffer_1_out), .out(multiplexer_7_out), .sel(draw_t));
  Register #(.width(16)) register_11 (.D(multiplexer_7_out), .Q(register_11_q), .clk(or_9_out));  // open: en, clr
  or or_9 (or_9_out, and_10_out, and_11_out);
  and and_10 (and_10_out, comparator_3_lt, wait_t);
  Pull_Resistor pull_resistor_6 (.node(comparator_3_lt));
  not not_6 (not_6_out, draw_t);
  Adder #(.width(16)) adder_7 (.a(16'h1), .b(register_10_q), .out(adder_7_out));  // open: cin, cout
  Divider #(.width(16)) divider_2 (.a(x_t), .b(16'h2), .out(divider_2_out));  // open: upper, rem
  Divider #(.width(16)) divider_3 (.a(y_t), .b(16'h2), .out(divider_3_out));  // open: upper, rem
  not not_7 (not_7_out, draw_t);
  Multiplier #(.width(16)) multiplier_3 (.a(16'h8), .b(adder_7_out), .out(multiplier_3_out));  // open: cin, cout
  // Probe on x_col
  // Probe on subtractor_1_out
  Subtractor #(.width(16)) subtractor_1 (.a(x_col), .b(divider_2_out), .out(subtractor_1_out));  // open: bin, bout
  // Probe on divider_2_out
  // Probe on divider_4_rem
  Subtractor #(.width(16)) subtractor_2 (.a(y_col), .b(divider_3_out), .out(subtractor_2_out));  // open: bin, bout
  and and_11 (and_11_out, not_7_out, clock);
  Negator #(.width(16)) negator_2 (.in(multiplier_4_out), .out(negator_2_out));
  Multiplier #(.width(16)) multiplier_4 (.a(register_11_q), .b(16'ha), .out(multiplier_4_out));  // open: cin, cout
  Subtractor #(.width(16)) subtractor_3 (.a(16'h3b), .b(multiplier_3_out), .out(subtractor_3_out));  // open: bin, bout
  Divider #(.width(16)) divider_4 (
    .a(subtractor_1_out), .b(16'h5), .out(divider_4_out), .rem(divider_4_rem));  // open: upper
  Divider #(.width(16)) divider_5 (
    .a(subtractor_2_out), .b(16'h5), .out(divider_5_out), .rem(divider_5_rem));  // open: upper
  Comparator #(.width(16), .mode("unsigned")) comparator_5 (
    .a(divider_4_rem), .b(16'h2), .eq(comparator_5_eq), .lt(comparator_5_lt));  // open: gt
  or or_10 (or_10_out, comparator_5_eq, comparator_5_lt);
  Multiplier #(.width(16)) multiplier_5 (.a(divider_5_out), .b(16'h5), .out(multiplier_5_out));  // open: cin, cout
  Comparator #(.width(16), .mode("unsigned")) comparator_6 (
    .a(divider_5_rem), .b(16'h2), .eq(comparator_6_eq), .lt(comparator_6_lt));  // open: gt
  or or_11 (or_11_out, comparator_6_eq, comparator_6_lt);
  Comparator #(.width(16), .mode("unsigned")) comparator_7 (
    .a(divider_4_out), .b(16'h6), .lt(x_aligned));  // open: gt, eq
  // Probe on divider_4_out
  and and_12 (and_12_out, or_10_out, or_11_out);
  // Probe on multiplier_5_out
  // Probe on adder_8_out
  Adder #(.width(16)) adder_8 (.a(divider_4_out), .b(multiplier_5_out), .out(adder_8_out));  // open: cin, cout
  Bit_Extender #(.in_width(16), .out_width(5)) bit_extender_2 (.in(adder_8_out), .out(col_adr));
  Comparator #(.width(16), .mode("unsigned")) comparator_8 (
    .a(adder_8_out), .b(16'he), .eq(comparator_8_eq), .lt(comparator_8_lt));  // open: gt
  or or_12 (or_12_out, comparator_8_eq, comparator_8_lt);
  and and_13 (may_collide, or_12_out, and_12_out, collide_check, x_aligned);

  // Other names for the same wires on the sheet: clk = clock

  // Notes on the sheet:
  //   enemy matrix
  //   enemies in row
  //   base texture id1
  //   base texture id2
  //   rows delta
  //   columns delta
  //   output X
  //   output Y
endmodule
module wall_multiobject (
  input  collide_check,
  input  \wait ,
  input  end_cycle,
  input  draw,
  input  [15:0] start_x,
  input  [15:0] x_col,
  input  [15:0] start_y,
  input  clock,
  input  [15:0] y_col,
  output [15:0] collided,
  output [15:0] id,
  output initing,
  output [15:0] y,
  output [4:0] DEBUG__wall_cout,
  output [15:0] x,
  output [15:0] command,
  output ready
);

  wire alive, and_1_out, and_2_out, and_3_out, and_5_out, and_6_out, and_7_out, block, comparator_1_eq,
       comparator_2_eq, comparator_3_gt, comparator_4_lt, comparator_5_eq, comparator_5_lt,
       controlled_buffer_1_out, counter_1_carry, d_ff_1_q, draw_t, may_collide, multiplexer_1_out, not_1_out,
       not_2_out, not_4_out, not_5_out, not_6_out, not_7_out, not_9_out, or_1_out, or_2_out, or_4_out,
       or_5_out, or_6_out, pull_resistor_1_node, register_1_q, register_3_q, register_4_q, register_5_q,
       texture_state, wait_t, xnor_1_out;
  wire [1:0] multiplexer_3_out, ram_1_data, subtractor_1_out, transistor_3_out;
  wire [4:0] col_adr, counter_1_q;
  wire [15:0] adder_1_out, adder_2_out, bit_extender_1_out, bit_extender_2_out, divider_1_out, divider_2_out,
       divider_3_out, multiplexer_4_out, multiplier_1_out, subtractor_2_out, subtractor_3_out, x_t, y_t;

  not not_1 (not_1_out, may_collide);
  or or_1 (or_1_out, end_cycle, ready);
  and and_1 (and_1_out, d_ff_1_q, alive);
  D_Flip_Flop #(.trigger("falling")) d_ff_1 (
    .clk(clock), .D(may_collide), .Q(d_ff_1_q), .reset(not_1_out));  // open: Qn, preset, en
  Register #(.width(1)) register_1 (.D(or_2_out), .Q(register_1_q), .clk(clock));  // open: en, clr
  or or_2 (or_2_out, collide_check, \wait );
  Register #(.width(1)) register_2 (.D(register_3_q), .Q(draw_t), .clk(clock), .clr(or_1_out));  // open: en
  Register #(.width(1)) register_3 (.D(draw), .Q(register_3_q), .clk(draw), .clr(or_1_out));  // open: en
  Counter #(.width(5), .max('h1)) counter_1 (
    .Q(counter_1_q), .carry(counter_1_carry), .clk(not_2_out));  // open: load, D, count, clr
  or or_3 (wait_t, register_1_q, or_2_out);
  and and_2 (and_2_out, and_1_out, ~block);  // AND_Gate
  D_Flip_Flop #(.trigger("falling")) d_ff_2 (.clk(clock), .D(and_1_out), .Q(block));  // open: Qn, preset, en, reset
  not not_2 (not_2_out, multiplexer_1_out);
  Multiplexer #(.enable("false")) multiplexer_1 (
    .in0(clock), .in1(pull_resistor_1_node), .out(multiplexer_1_out), .sel(register_4_q));
  Pull_Resistor pull_resistor_1 (.node(pull_resistor_1_node));
  Transistor #(.\type ("n"), .gate("br")) transistor_1 (.in(or_4_out), .out(pull_resistor_1_node), .gate(draw_t));
  or or_4 (or_4_out, wait_t, and_3_out);
  Transistor #(.\type ("n"), .width(16)) transistor_2 (.in(16'h3), .out(collided), .gate(and_2_out));
  not not_3 (initing, register_4_q);
  Multiplexer #(.width(5), .enable("false")) multiplexer_2 (
    .in0(counter_1_q), .in1(col_adr), .out(DEBUG__wall_cout), .sel(may_collide));
  not not_4 (not_4_out, counter_1_carry);
  Register #(.width(1)) register_4 (.D(not_4_out), .Q(register_4_q), .clk(not_4_out));  // open: en, clr
  and and_3 (and_3_out, ~clock, ~and_5_out);  // AND_Gate
  Transistor #(.gate("br"), .width(2)) transistor_3 (.in(2'b11), .out(transistor_3_out), .gate(register_4_q));
  Transistor #(.\type ("n"), .width(2)) transistor_4 (
    .in(multiplexer_3_out), .out(transistor_3_out), .gate(register_4_q));
  assign bit_extender_1_out = {{11{1'b0}}, DEBUG__wall_cout};  // Bit_Extender bit_extender_1
  assign controlled_buffer_1_out = not_5_out ? clock : 1'bz;  // Controlled_Buffer controlled_buffer_1
  xnor xnor_1 (xnor_1_out, may_collide, register_4_q);
  Register #(.width(1)) register_5 (.D(not_4_out), .Q(register_5_q), .clk(not_4_out), .clr(register_5_q));  // open: en
  RAM #(.addrWidth(5), .dataWidth(2), .bus("separate")) ram_1 (
    .addr(DEBUG__wall_cout), .din(transistor_3_out), .data(ram_1_data), .str(xnor_1_out),
    .clk(controlled_buffer_1_out));  // open: sel, ld, clr
  not not_5 (not_5_out, block);
  Comparator #(.width(2), .mode("unsigned")) comparator_1 (
    .a(ram_1_data), .b(2'b00), .eq(comparator_1_eq));  // open: gt, lt
  and and_4 (ready, register_5_q, draw_t);
  Register #(.width(16)) register_6 (.D(start_x), .Q(x_t), .clk(not_6_out));  // open: en, clr
  not not_6 (not_6_out, initing);
  Register #(.width(16)) register_7 (.D(start_y), .Q(y_t), .clk(not_7_out));  // open: en, clr
  not not_7 (not_7_out, initing);
  assign bit_extender_2_out = {{14{1'b0}}, ram_1_data};  // Bit_Extender bit_extender_2
  Subtractor #(.width(2)) subtractor_1 (.a(ram_1_data), .b(2'b01), .out(subtractor_1_out));  // open: bin, bout
  Multiplexer #(.width(2), .enable("false")) multiplexer_3 (
    .in0(subtractor_1_out), .in1(2'b00), .out(multiplexer_3_out), .sel(comparator_1_eq));
  Comparator #(.width(2), .mode("unsigned")) comparator_2 (
    .a(ram_1_data), .b(2'b00), .eq(comparator_2_eq));  // open: gt, lt
  not not_8 (alive, comparator_2_eq);
  and and_5 (and_5_out, alive, register_4_q);
  Counter #(.width(1), .max('h1)) counter_2 (
    .Q(texture_state), .clk(register_5_q));  // open: load, D, count, carry, clr
  Multiplexer #(.width(16), .enable("false")) multiplexer_4 (
    .in0({16{1'b0}}), .in1(16'h1), .out(multiplexer_4_out), .sel(and_6_out));
  and and_6 (and_6_out, and_5_out, or_5_out);
  or or_5 (or_5_out, not_9_out, wait_t);
  not not_9 (not_9_out, clock);
  Adder #(.width(16)) adder_1 (.a(16'h10), .b(bit_extender_2_out), .out(adder_1_out));  // open: cin, cout
  Multiplier #(.width(16)) multiplier_1 (.a(bit_extender_1_out), .b(16'h4), .out(multiplier_1_out));  // open: cin, cout
  assign id = draw_t ? adder_1_out : 16'bz;  // Controlled_Buffer controlled_buffer_2
  assign y = draw_t ? y_t : 16'bz;  // Controlled_Buffer controlled_buffer_3
  assign x = draw_t ? adder_2_out : 16'bz;  // Controlled_Buffer controlled_buffer_4
  Adder #(.width(16)) adder_2 (.a(x_t), .b(multiplier_1_out), .out(adder_2_out));  // open: cin, cout
  assign command = draw_t ? multiplexer_4_out : 16'bz;  // Controlled_Buffer controlled_buffer_5
  Pull_Resistor pull_resistor_2 (.node(x_col));
  Pull_Resistor pull_resistor_3 (.node(y_col));
  // Probe on x_col
  Subtractor #(.width(16)) subtractor_2 (.a(x_col), .b(divider_1_out), .out(subtractor_2_out));  // open: bin, bout
  Divider #(.width(16)) divider_1 (.a(x_t), .b(16'h2), .out(divider_1_out));  // open: upper, rem
  // Probe on divider_1_out
  Subtractor #(.width(16)) subtractor_3 (.a(y_col), .b(divider_2_out), .out(subtractor_3_out));  // open: bin, bout
  Divider #(.width(16)) divider_2 (.a(y_t), .b(16'h2), .out(divider_2_out));  // open: upper, rem
  // Probe on subtractor_2_out
  Divider #(.width(16)) divider_3 (.a(subtractor_2_out), .b(16'h2), .out(divider_3_out));  // open: upper, rem
  Comparator #(.width(16)) comparator_3 (.a(subtractor_3_out), .b(16'hfffd), .gt(comparator_3_gt));  // open: eq, lt
  Comparator #(.width(16)) comparator_4 (.a(subtractor_3_out), .b(16'h3), .lt(comparator_4_lt));  // open: gt, eq
  // Probe on divider_3_out
  // Probe on divider_3_out
  and and_7 (and_7_out, comparator_3_gt, comparator_4_lt);
  Comparator #(.width(16), .mode("unsigned")) comparator_5 (
    .a(divider_3_out), .b(16'h1), .eq(comparator_5_eq), .lt(comparator_5_lt));  // open: gt
  Bit_Extender #(.in_width(16), .out_width(5)) bit_extender_3 (.in(divider_3_out), .out(col_adr));
  or or_6 (or_6_out, comparator_5_eq, comparator_5_lt);
  and and_8 (may_collide, or_6_out, collide_check, and_7_out);

  // Other names for the same wires on the sheet: clk = clock

  // Notes on the sheet:
  //   wall matrix
  //   base texture id
  //   columns delta
  //   output Y
  //   output X
endmodule

module win_multiobject (
  input  \wait ,
  input  draw,
  input  clock,
  output [15:0] id,
  output [15:0] x,
  output [15:0] y,
  output [15:0] command,
  output ready
);

  wire and_1_out, comparator_1_eq, draw_t, not_1_out, not_2_out, register_2_q, transistor_1_out;
  wire [3:0] counter_1_q;
  wire [15:0] bit_extender_1_out, multiplexer_1_out, multiplexer_2_out, multiplexer_3_out, multiplexer_4_out;

  Register #(.width(1)) register_1 (.D(register_2_q), .Q(draw_t), .clk(not_1_out), .clr(ready));  // open: en
  Register #(.width(1)) register_2 (.D(draw), .Q(register_2_q), .clk(draw), .clr(ready));  // open: en
  not not_1 (not_1_out, clock);
  not not_2 (not_2_out, \wait );
  Counter #(.width(4), .max('h5)) counter_1 (
    .Q(counter_1_q), .carry(ready), .clk(transistor_1_out), .clr(ready));  // open: load, D, count
  Transistor #(.\type ("n")) transistor_1 (.in(clock), .out(transistor_1_out), .gate(and_1_out));
  and and_1 (and_1_out, not_2_out, draw_t);
  Multiplexer #(.width(16), .enable("false")) multiplexer_1 (
    .in0(16'hb), .in1(16'hc), .out(multiplexer_1_out), .sel(counter_1_q[1]));
  Multiplexer #(.width(16), .enable("false")) multiplexer_2 (
    .in0(16'h1a), .in1(16'h20), .out(multiplexer_2_out), .sel(counter_1_q[1]));
  Comparator #(.width(4), .mode("unsigned")) comparator_1 (
    .a(counter_1_q), .b(4'b0000), .eq(comparator_1_eq));  // open: gt, lt
  assign bit_extender_1_out = {{15{1'b0}}, counter_1_q[0]};  // Bit_Extender bit_extender_1
  assign id = draw_t ? multiplexer_1_out : 16'bz;  // Controlled_Buffer controlled_buffer_1
  assign x = draw_t ? 16'h10 : 16'bz;  // Controlled_Buffer controlled_buffer_2
  assign y = draw_t ? multiplexer_2_out : 16'bz;  // Controlled_Buffer controlled_buffer_3
  Multiplexer #(.width(16), .enable("false")) multiplexer_3 (
    .in0(multiplexer_4_out), .in1(16'h2), .out(multiplexer_3_out), .sel(comparator_1_eq));
  Multiplexer #(.width(16), .enable("false")) multiplexer_4 (
    .in0(bit_extender_1_out), .in1(16'h2), .out(multiplexer_4_out), .sel(counter_1_q[2]));
  assign command = draw_t ? multiplexer_3_out : 16'bz;  // Controlled_Buffer controlled_buffer_4

  // Other names for the same wires on the sheet: clk = clock
endmodule

module lose_multiobject (
  input  \wait ,
  input  draw,
  input  clock,
  output [15:0] id,
  output [15:0] x,
  output [15:0] y,
  output [15:0] command,
  output ready
);

  wire and_1_out, comparator_1_eq, draw_t, not_1_out, not_2_out, register_2_q, transistor_1_out;
  wire [3:0] counter_1_q;
  wire [15:0] bit_extender_1_out, multiplexer_1_out, multiplexer_2_out, multiplexer_3_out, multiplexer_4_out;

  Register #(.width(1)) register_1 (.D(register_2_q), .Q(draw_t), .clk(not_1_out), .clr(ready));  // open: en
  Register #(.width(1)) register_2 (.D(draw), .Q(register_2_q), .clk(draw), .clr(ready));  // open: en
  not not_1 (not_1_out, clock);
  not not_2 (not_2_out, \wait );
  Counter #(.width(4), .max('hf)) counter_1 (
    .Q(counter_1_q), .carry(ready), .clk(transistor_1_out), .clr(ready));  // open: load, D, count
  Transistor #(.\type ("n")) transistor_1 (.in(clock), .out(transistor_1_out), .gate(and_1_out));
  and and_1 (and_1_out, not_2_out, draw_t);
  Multiplexer #(.width(16), .enable("false")) multiplexer_1 (
    .in0(16'hd), .in1(16'he), .out(multiplexer_1_out), .sel(counter_1_q[1]));
  Multiplexer #(.width(16), .enable("false")) multiplexer_2 (
    .in0(16'h1a), .in1(16'h20), .out(multiplexer_2_out), .sel(counter_1_q[1]));
  Comparator #(.width(4), .mode("unsigned")) comparator_1 (
    .a(counter_1_q), .b(4'b0000), .eq(comparator_1_eq));  // open: gt, lt
  assign bit_extender_1_out = {{15{1'b0}}, counter_1_q[0]};  // Bit_Extender bit_extender_1
  assign id = draw_t ? multiplexer_1_out : 16'bz;  // Controlled_Buffer controlled_buffer_1
  assign x = draw_t ? 16'h8 : 16'bz;  // Controlled_Buffer controlled_buffer_2
  assign y = draw_t ? multiplexer_2_out : 16'bz;  // Controlled_Buffer controlled_buffer_3
  Multiplexer #(.width(16), .enable("false")) multiplexer_3 (
    .in0(multiplexer_4_out), .in1(16'h2), .out(multiplexer_3_out), .sel(comparator_1_eq));
  Multiplexer #(.width(16), .enable("false")) multiplexer_4 (
    .in0(bit_extender_1_out), .in1(16'h2), .out(multiplexer_4_out), .sel(counter_1_q[2]));
  assign command = draw_t ? multiplexer_3_out : 16'bz;  // Controlled_Buffer controlled_buffer_4

  // Other names for the same wires on the sheet: clk = clock
endmodule

module enemy_writer (
  input  [15:0] y,
  input  [15:0] x,
  input  run,
  input  clock,
  output [15:0] val,
  output [15:0] adr,
  output write
);

  wire activate_q, counter_1_carry, not_1_out, not_2_out, pull_resistor_1_node, writing;
  wire [2:0] counter_1_q, random_1_out;
  wire [15:0] bit_extender_1_out, multiplexer_1_out, multiplexer_2_out;

  Pull_Resistor pull_resistor_1 (.node(pull_resistor_1_node));
  assign pull_resistor_1_node = writing ? clock : 1'bz;  // Controlled_Buffer controlled_buffer_1
  Random #(.width(3)) random_1 (.clk(pull_resistor_1_node), .out(random_1_out));  // open: next, clr
  assign bit_extender_1_out = {{13{1'b0}}, random_1_out};  // Bit_Extender bit_extender_1
  Counter #(.width(3), .max('h5)) counter_1 (
    .Q(counter_1_q), .carry(counter_1_carry), .clk(not_1_out), .clr(not_2_out));  // open: load, D, count
  not not_1 (not_1_out, clock);
  Multiplexer #(.select(3), .width(16), .enable("false")) multiplexer_1 (
    .in0({16{1'b0}}), .in1(16'h80), .in2(16'h82), .in3(16'hac), .in4(16'h84), .out(multiplexer_1_out),
    .sel(counter_1_q));  // open: in5, in6, in7
  Multiplexer #(.select(3), .width(16), .enable("false")) multiplexer_2 (
    .in0({16{1'b0}}), .in1(x), .in2(y), .in3(bit_extender_1_out), .in4(16'h1), .out(multiplexer_2_out),
    .sel(counter_1_q));  // open: in5, in6, in7
  D_Flip_Flop activate (.clk(run), .D(run), .Q(activate_q), .reset(counter_1_carry));  // open: Qn, preset, en
  assign adr = writing ? multiplexer_1_out : 16'bz;  // Controlled_Buffer controlled_buffer_2
  // Probe on multiplexer_1_out
  assign val = writing ? multiplexer_2_out : 16'bz;  // Controlled_Buffer controlled_buffer_3
  // Probe on multiplexer_2_out
  not not_2 (not_2_out, writing);
  buf buffer_1 (write, writing);
  D_Flip_Flop #(.trigger("falling")) synchronizer (
    .clk(clock), .D(activate_q), .Q(writing), .reset(counter_1_carry));  // open: Qn, preset, en

  // Other names for the same wires on the sheet: clk = clock

  // Notes on the sheet:
  //   buffer_1 drives only 1 and floats otherwise
endmodule

module check2_writer (
  input  run,
  input  clock,
  input  sync,
  output [15:0] adr,
  output [15:0] val,
  output write
);

  wire activator_q, counter_1_carry, not_1_out, writing;
  wire [1:0] counter_1_q;
  wire [15:0] multiplexer_1_out, multiplexer_2_out;

  Counter #(.width(2), .max('h2)) counter_1 (
    .Q(counter_1_q), .carry(counter_1_carry), .clk(clock), .clr(not_1_out));  // open: load, D, count
  Multiplexer #(.select(2), .width(16), .enable("false")) multiplexer_1 (
    .in0({16{1'b0}}), .in1(16'h84), .out(multiplexer_1_out), .sel(counter_1_q));  // open: in2, in3
  Multiplexer #(.select(2), .width(16), .enable("false")) multiplexer_2 (
    .in0({16{1'b0}}), .in1(16'h2), .out(multiplexer_2_out), .sel(counter_1_q));  // open: in2, in3
  D_Flip_Flop activator (.clk(run), .D(run), .Q(activator_q), .reset(counter_1_carry));  // open: Qn, preset, en
  // Probe on multiplexer_1_out
  assign adr = writing ? multiplexer_1_out : 16'bz;  // Controlled_Buffer controlled_buffer_1
  assign val = writing ? multiplexer_2_out : 16'bz;  // Controlled_Buffer controlled_buffer_2
  // Probe on multiplexer_2_out
  not not_1 (not_1_out, writing);
  D_Flip_Flop #(.trigger("high")) synchronizer (
    .clk(sync), .D(activator_q), .Q(writing), .reset(counter_1_carry));  // open: Qn, preset, en
  buf buffer_1 (write, activator_q);
  buf buffer_2 (write, writing);

  // Other names for the same wires on the sheet: clk = clock

  // Notes on the sheet:
  //   buffer_1 drives only 1 and floats otherwise
  //   buffer_2 drives only 1 and floats otherwise
endmodule

module speed_writer (
  input  [15:0] speed,
  input  clock,
  input  run,
  output [15:0] adr,
  output [15:0] val,
  output write
);

  wire activator_q, and_1_out, comparator_1_eq, counter_1_carry, not_1_out, not_2_out, writing;
  wire [1:0] counter_1_q;
  wire [15:0] multiplexer_1_out, multiplexer_2_out, register_1_q;

  Register #(.width(16)) register_1 (.D(speed), .Q(register_1_q), .clk(and_1_out));  // open: en, clr
  and and_1 (and_1_out, run, not_1_out);
  Counter #(.width(2), .max('h2)) counter_1 (
    .Q(counter_1_q), .carry(counter_1_carry), .clk(clock), .clr(not_2_out));  // open: load, D, count
  Comparator #(.width(16), .mode("unsigned")) comparator_1 (
    .a(register_1_q), .b(speed), .eq(comparator_1_eq));  // open: gt, lt
  not not_1 (not_1_out, comparator_1_eq);
  Multiplexer #(.select(2), .width(16), .enable("false")) multiplexer_1 (
    .in0({16{1'b0}}), .in1(16'h98), .out(multiplexer_1_out), .sel(counter_1_q));  // open: in2, in3
  Multiplexer #(.select(2), .width(16), .enable("false")) multiplexer_2 (
    .in0({16{1'b0}}), .in1(speed), .out(multiplexer_2_out), .sel(counter_1_q));  // open: in2, in3
  // Probe on multiplexer_1_out
  assign adr = writing ? multiplexer_1_out : 16'bz;  // Controlled_Buffer controlled_buffer_1
  assign val = writing ? multiplexer_2_out : 16'bz;  // Controlled_Buffer controlled_buffer_2
  // Probe on multiplexer_2_out
  not not_2 (not_2_out, writing);
  D_Flip_Flop activator (
    .clk(and_1_out), .D(and_1_out), .Q(activator_q), .reset(counter_1_carry));  // open: Qn, preset, en
  buf buffer_1 (write, writing);
  D_Flip_Flop #(.trigger("falling")) synchronizer (
    .clk(clock), .D(activator_q), .Q(writing), .reset(counter_1_carry));  // open: Qn, preset, en

  // Other names for the same wires on the sheet: clk = clock

  // Notes on the sheet:
  //   buffer_1 drives only 1 and floats otherwise
endmodule

module shot_writer (
  input  [15:0] x,
  input  [15:0] y,
  input  run,
  input  clock,
  output [15:0] adr,
  output [15:0] val,
  output write
);

  wire activator_q, counter_1_carry, not_1_out, not_2_out, writing;
  wire [1:0] bit_extender_1_out;
  wire [2:0] counter_1_q;
  wire [15:0] multiplexer_1_out, multiplexer_2_out;

  // Probe on x
  // Probe on y
  Counter #(.width(3), .max('h4)) counter_1 (
    .Q(counter_1_q), .carry(counter_1_carry), .clk(not_1_out), .clr(not_2_out));  // open: load, D, count
  not not_1 (not_1_out, clock);
  Bit_Extender #(.in_width(3), .out_width(2)) bit_extender_1 (.in(counter_1_q), .out(bit_extender_1_out));
  Multiplexer #(.select(2), .width(16), .enable("false")) multiplexer_1 (
    .in0({16{1'b0}}), .in1(16'ha8), .in2(16'haa), .in3(16'ha0), .out(multiplexer_1_out),
    .sel(bit_extender_1_out));
  Multiplexer #(.select(2), .width(16), .enable("false")) multiplexer_2 (
    .in0({16{1'b0}}), .in1(x), .in2(y), .in3(16'h1), .out(multiplexer_2_out), .sel(bit_extender_1_out));
  // Probe on multiplexer_1_out
  assign adr = writing ? multiplexer_1_out : 16'bz;  // Controlled_Buffer controlled_buffer_1
  assign val = writing ? multiplexer_2_out : 16'bz;  // Controlled_Buffer controlled_buffer_2
  // Probe on multiplexer_2_out
  not not_2 (not_2_out, writing);
  D_Flip_Flop activator (.clk(run), .D(run), .Q(activator_q), .reset(counter_1_carry));  // open: Qn, preset, en
  buf buffer_1 (write, writing);
  D_Flip_Flop #(.trigger("falling")) synchronizer (
    .clk(clock), .D(activator_q), .Q(writing), .reset(counter_1_carry));  // open: Qn, preset, en

  // Other names for the same wires on the sheet: clk = clock

  // Notes on the sheet:
  //   buffer_1 drives only 1 and floats otherwise
endmodule

module player_writer (
  input  [15:0] x,
  input  [15:0] y,
  input  run,
  input  clock,
  output [15:0] adr,
  output [15:0] val,
  output write
);

  wire activator_q, counter_1_carry, not_1_out, not_2_out, writing;
  wire [1:0] bit_extender_1_out;
  wire [2:0] counter_1_q;
  wire [15:0] multiplexer_1_out, multiplexer_2_out;

  Counter #(.width(3), .max('h3)) counter_1 (
    .Q(counter_1_q), .carry(counter_1_carry), .clk(not_1_out), .clr(not_2_out));  // open: load, D, count
  not not_1 (not_1_out, clock);
  // Probe on x
  // Probe on y
  Bit_Extender #(.in_width(3), .out_width(2)) bit_extender_1 (.in(counter_1_q), .out(bit_extender_1_out));
  Multiplexer #(.select(2), .width(16), .enable("false")) multiplexer_1 (
    .in0({16{1'b0}}), .in1(16'ha8), .in2(16'haa), .out(multiplexer_1_out), .sel(bit_extender_1_out));  // open: in3
  Multiplexer #(.select(2), .width(16), .enable("false")) multiplexer_2 (
    .in0({16{1'b0}}), .in1(x), .in2(y), .out(multiplexer_2_out), .sel(bit_extender_1_out));  // open: in3
  D_Flip_Flop activator (.clk(run), .D(run), .Q(activator_q), .reset(counter_1_carry));  // open: Qn, preset, en
  assign adr = writing ? multiplexer_1_out : 16'bz;  // Controlled_Buffer controlled_buffer_1
  // Probe on multiplexer_1_out
  assign val = writing ? multiplexer_2_out : 16'bz;  // Controlled_Buffer controlled_buffer_2
  // Probe on multiplexer_2_out
  not not_2 (not_2_out, writing);
  D_Flip_Flop #(.trigger("falling")) synchronizer (
    .clk(clock), .D(activator_q), .Q(writing), .reset(counter_1_carry));  // open: Qn, preset, en
  buf buffer_1 (write, writing);

  // Other names for the same wires on the sheet: clk = clock

  // Notes on the sheet:
  //   buffer_1 drives only 1 and floats otherwise
endmodule

module collision_writer (
  input  [15:0] collided,
  input  run,
  input  clock,
  output [15:0] adr,
  output [15:0] val,
  output write
);

  wire activator_q, counter_1_carry, not_1_out, not_2_out, writing;
  wire [1:0] counter_1_q;
  wire [15:0] multiplexer_1_out, multiplexer_2_out;

  Counter #(.width(2), .max('h2)) counter_1 (
    .Q(counter_1_q), .carry(counter_1_carry), .clk(not_1_out), .clr(not_2_out));  // open: load, D, count
  not not_1 (not_1_out, clock);
  Multiplexer #(.select(2), .width(16), .enable("false")) multiplexer_1 (
    .in0({16{1'b0}}), .in1(16'h94), .out(multiplexer_1_out), .sel(counter_1_q));  // open: in2, in3
  Multiplexer #(.select(2), .width(16), .enable("false")) multiplexer_2 (
    .in0({16{1'b0}}), .in1(collided), .out(multiplexer_2_out), .sel(counter_1_q));  // open: in2, in3
  assign adr = writing ? multiplexer_1_out : 16'bz;  // Controlled_Buffer controlled_buffer_1
  // Probe on multiplexer_1_out
  assign val = writing ? multiplexer_2_out : 16'bz;  // Controlled_Buffer controlled_buffer_2
  // Probe on multiplexer_2_out
  not not_2 (not_2_out, writing);
  D_Flip_Flop activator (.clk(run), .D(run), .Q(activator_q), .reset(counter_1_carry));  // open: Qn, preset, en
  buf buffer_1 (write, writing);
  D_Flip_Flop #(.trigger("falling")) synchronizer (
    .clk(clock), .D(activator_q), .Q(writing), .reset(counter_1_carry));  // open: Qn, preset, en

  // Other names for the same wires on the sheet: clk = clock

  // Notes on the sheet:
  //   buffer_1 drives only 1 and floats otherwise
endmodule

module simple_drawer_32x32 (
  input  [4:0] texture_line,
  input  [31:0] texture_input,
  input  [4:0] x,
  input  [4:0] y,
  output [4:0] cur_line,
  output [31:0] line_x1
);

  wire [31:0] n32_bit_reverse_1_out_2;

  // Probe on x
  // Probe on y
  Adder #(.width(5)) adder_1 (.a(texture_line), .b(y), .out(cur_line));  // open: cin, cout
  _32_bit_reverse u_32_bit_reverse_1 (.in_1(texture_input), .out_2(n32_bit_reverse_1_out_2));
  Pull_Resistor pull_resistor_1 (.node(x));
  Shifter #(.width(32), .shift("lr")) shifter_1 (.in(n32_bit_reverse_1_out_2), .\dist (x), .out(line_x1));
endmodule

module video_buffer_32x32 (
  input  write,
  input  [31:0] \input ,
  input  [4:0] y,
  input  show,
  output [31:0] out_5,
  output [31:0] out_6,
  output [31:0] out_7,
  output [31:0] out_8,
  output [31:0] out_9,
  output [31:0] out_10,
  output [31:0] out_11,
  output [31:0] out_12,
  output [31:0] out_13,
  output [31:0] out_14,
  output [31:0] out_15,
  output [31:0] out_16,
  output [31:0] out_17,
  output [31:0] out_18,
  output [31:0] out_19,
  output [31:0] out_20,
  output [31:0] out_21,
  output [31:0] out_22,
  output [31:0] out_23,
  output [31:0] out_24,
  output [31:0] out_25,
  output [31:0] out_26,
  output [31:0] out_27,
  output [31:0] out_28,
  output [31:0] out_29,
  output [31:0] out_30,
  output [31:0] out_31,
  output [31:0] out_32,
  output [31:0] out_33,
  output [31:0] out_34,
  output [31:0] out_35,
  output [31:0] out_36
);

  wire _0, _1, _2, _3, _4, _5, _6, _7, _8, _9, _10, _11, _12, _13, _14, _15, _16, _17, _18, _19, _20, _21,
       _22, _23, _24, _25, _26, _27, _28, _29, _30, _31;

  Decoder #(.select(5), .disabled(0)) decoder_1 (
    .out0(_0), .out1(_1), .out2(_2), .out3(_3), .out4(_4), .out5(_5), .out6(_6), .out7(_7), .out8(_8),
    .out9(_9), .out10(_10), .out11(_11), .out12(_12), .out13(_13), .out14(_14), .out15(_15), .out16(_16),
    .out17(_17), .out18(_18), .out19(_19), .out20(_20), .out21(_21), .out22(_22), .out23(_23), .out24(_24),
    .out25(_25), .out26(_26), .out27(_27), .out28(_28), .out29(_29), .out30(_30), .out31(_31), .sel(y),
    .en(write));
  _32buffer_el u_32buffer_el_1 (
    .\input (\input ), ._1___buffer_read(_0), .video(out_5), ._1___buffer_write___clr(show));
  _32buffer_el u_32buffer_el_2 (
    .\input (\input ), ._1___buffer_read(_1), .video(out_6), ._1___buffer_write___clr(show));
  _32buffer_el u_32buffer_el_3 (
    .\input (\input ), ._1___buffer_read(_2), .video(out_7), ._1___buffer_write___clr(show));
  _32buffer_el u_32buffer_el_4 (
    .\input (\input ), ._1___buffer_read(_3), .video(out_8), ._1___buffer_write___clr(show));
  _32buffer_el u_32buffer_el_5 (
    .\input (\input ), ._1___buffer_read(_4), .video(out_9), ._1___buffer_write___clr(show));
  _32buffer_el u_32buffer_el_6 (
    .\input (\input ), ._1___buffer_read(_5), .video(out_10), ._1___buffer_write___clr(show));
  _32buffer_el u_32buffer_el_7 (
    .\input (\input ), ._1___buffer_read(_6), .video(out_11), ._1___buffer_write___clr(show));
  _32buffer_el u_32buffer_el_8 (
    .\input (\input ), ._1___buffer_read(_7), .video(out_12), ._1___buffer_write___clr(show));
  _32buffer_el u_32buffer_el_9 (
    .\input (\input ), ._1___buffer_read(_8), .video(out_13), ._1___buffer_write___clr(show));
  _32buffer_el u_32buffer_el_10 (
    .\input (\input ), ._1___buffer_read(_9), .video(out_14), ._1___buffer_write___clr(show));
  _32buffer_el u_32buffer_el_11 (
    .\input (\input ), ._1___buffer_read(_10), .video(out_15), ._1___buffer_write___clr(show));
  _32buffer_el u_32buffer_el_12 (
    .\input (\input ), ._1___buffer_read(_11), .video(out_16), ._1___buffer_write___clr(show));
  _32buffer_el u_32buffer_el_13 (
    .\input (\input ), ._1___buffer_read(_12), .video(out_17), ._1___buffer_write___clr(show));
  _32buffer_el u_32buffer_el_14 (
    .\input (\input ), ._1___buffer_read(_13), .video(out_18), ._1___buffer_write___clr(show));
  _32buffer_el u_32buffer_el_15 (
    .\input (\input ), ._1___buffer_read(_14), .video(out_19), ._1___buffer_write___clr(show));
  _32buffer_el u_32buffer_el_16 (
    .\input (\input ), ._1___buffer_read(_15), .video(out_20), ._1___buffer_write___clr(show));
  _32buffer_el u_32buffer_el_17 (
    .\input (\input ), ._1___buffer_read(_16), .video(out_21), ._1___buffer_write___clr(show));
  _32buffer_el u_32buffer_el_18 (
    .\input (\input ), ._1___buffer_read(_17), .video(out_22), ._1___buffer_write___clr(show));
  _32buffer_el u_32buffer_el_19 (
    .\input (\input ), ._1___buffer_read(_18), .video(out_23), ._1___buffer_write___clr(show));
  _32buffer_el u_32buffer_el_20 (
    .\input (\input ), ._1___buffer_read(_19), .video(out_24), ._1___buffer_write___clr(show));
  _32buffer_el u_32buffer_el_21 (
    .\input (\input ), ._1___buffer_read(_20), .video(out_25), ._1___buffer_write___clr(show));
  _32buffer_el u_32buffer_el_22 (
    .\input (\input ), ._1___buffer_read(_21), .video(out_26), ._1___buffer_write___clr(show));
  _32buffer_el u_32buffer_el_23 (
    .\input (\input ), ._1___buffer_read(_22), .video(out_27), ._1___buffer_write___clr(show));
  _32buffer_el u_32buffer_el_24 (
    .\input (\input ), ._1___buffer_read(_23), .video(out_28), ._1___buffer_write___clr(show));
  _32buffer_el u_32buffer_el_25 (
    .\input (\input ), ._1___buffer_read(_24), .video(out_29), ._1___buffer_write___clr(show));
  _32buffer_el u_32buffer_el_26 (
    .\input (\input ), ._1___buffer_read(_25), .video(out_30), ._1___buffer_write___clr(show));
  _32buffer_el u_32buffer_el_27 (
    .\input (\input ), ._1___buffer_read(_26), .video(out_31), ._1___buffer_write___clr(show));
  _32buffer_el u_32buffer_el_28 (
    .\input (\input ), ._1___buffer_read(_27), .video(out_32), ._1___buffer_write___clr(show));
  _32buffer_el u_32buffer_el_29 (
    .\input (\input ), ._1___buffer_read(_28), .video(out_33), ._1___buffer_write___clr(show));
  _32buffer_el u_32buffer_el_30 (
    .\input (\input ), ._1___buffer_read(_29), .video(out_34), ._1___buffer_write___clr(show));
  _32buffer_el u_32buffer_el_31 (
    .\input (\input ), ._1___buffer_read(_30), .video(out_35), ._1___buffer_write___clr(show));
  _32buffer_el u_32buffer_el_32 (
    .\input (\input ), ._1___buffer_read(_31), .video(out_36), ._1___buffer_write___clr(show));

  // Other names for the same wires on the sheet: inp[31:0] = \input ; w = show

  // Notes on the sheet:
  //   write: pull=down
endmodule

module multilayer_video_buffer_32x32 (
  input  [31:0] in_1,
  input  [31:0] in_2,
  input  [31:0] in_3,
  input  [31:0] in_4,
  input  [31:0] in_5,
  input  [31:0] in_6,
  input  write,
  input  [31:0] in_8,
  input  [31:0] \input ,
  input  [4:0] y,
  input  show,
  input  [31:0] in_12,
  input  [31:0] in_13,
  input  [31:0] in_14,
  input  [31:0] in_15,
  input  [31:0] in_16,
  input  [31:0] in_17,
  input  [31:0] in_18,
  input  [31:0] in_19,
  input  [31:0] in_20,
  input  [31:0] in_21,
  input  [31:0] in_22,
  input  [31:0] in_23,
  input  [31:0] in_24,
  input  [31:0] in_25,
  input  [31:0] in_26,
  input  [31:0] in_27,
  input  [31:0] in_28,
  input  [31:0] in_29,
  input  [31:0] in_30,
  input  [31:0] in_31,
  input  [31:0] in_32,
  input  [31:0] in_33,
  input  [31:0] in_34,
  input  [31:0] in_35,
  input  [31:0] in_36,
  output [31:0] out_37,
  output [31:0] out_38,
  output [31:0] out_39,
  output [31:0] out_40,
  output [31:0] out_41,
  output [31:0] out_42,
  output [31:0] out_43,
  output [31:0] out_44,
  output [31:0] out_45,
  output [31:0] out_46,
  output [31:0] out_47,
  output [31:0] out_48,
  output [31:0] out_49,
  output [31:0] out_50,
  output [31:0] out_51,
  output [31:0] out_52,
  output [31:0] out_53,
  output [31:0] out_54,
  output [31:0] out_55,
  output [31:0] out_56,
  output [31:0] out_57,
  output [31:0] out_58,
  output [31:0] out_59,
  output [31:0] out_60,
  output [31:0] out_61,
  output [31:0] out_62,
  output [31:0] out_63,
  output [31:0] out_64,
  output [31:0] out_65,
  output [31:0] out_66,
  output [31:0] out_67,
  output [31:0] out_68
);

  wire _0, _1, _2, _3, _4, _5, _6, _7, _8, _9, _10, _11, _12, _13, _14, _15, _16, _17, _18, _19, _20, _21,
       _22, _23, _24, _25, _26, _27, _28, _29, _30, _31;
  wire [31:0] n32buffer_el_1_video, n32buffer_el_2_video, n32buffer_el_3_video, n32buffer_el_4_video,
       n32buffer_el_5_video, n32buffer_el_6_video, n32buffer_el_7_video, n32buffer_el_8_video,
       n32buffer_el_9_video, n32buffer_el_10_video, n32buffer_el_11_video, n32buffer_el_12_video,
       n32buffer_el_13_video, n32buffer_el_14_video, n32buffer_el_15_video, n32buffer_el_16_video,
       n32buffer_el_17_video, n32buffer_el_18_video, n32buffer_el_19_video, n32buffer_el_20_video,
       n32buffer_el_21_video, n32buffer_el_22_video, n32buffer_el_23_video, n32buffer_el_24_video,
       n32buffer_el_25_video, n32buffer_el_26_video, n32buffer_el_27_video, n32buffer_el_28_video,
       n32buffer_el_29_video, n32buffer_el_30_video, n32buffer_el_31_video, n32buffer_el_32_video;

  Decoder #(.select(5), .disabled(0)) decoder_1 (
    .out0(_0), .out1(_1), .out2(_2), .out3(_3), .out4(_4), .out5(_5), .out6(_6), .out7(_7), .out8(_8),
    .out9(_9), .out10(_10), .out11(_11), .out12(_12), .out13(_13), .out14(_14), .out15(_15), .out16(_16),
    .out17(_17), .out18(_18), .out19(_19), .out20(_20), .out21(_21), .out22(_22), .out23(_23), .out24(_24),
    .out25(_25), .out26(_26), .out27(_27), .out28(_28), .out29(_29), .out30(_30), .out31(_31), .sel(y),
    .en(write));
  _32buffer_el u_32buffer_el_1 (
    .\input (\input ), ._1___buffer_read(_0), .video(n32buffer_el_1_video), ._1___buffer_write___clr(show));
  _32buffer_el u_32buffer_el_2 (
    .\input (\input ), ._1___buffer_read(_1), .video(n32buffer_el_2_video), ._1___buffer_write___clr(show));
  _32buffer_el u_32buffer_el_3 (
    .\input (\input ), ._1___buffer_read(_2), .video(n32buffer_el_3_video), ._1___buffer_write___clr(show));
  _32buffer_el u_32buffer_el_4 (
    .\input (\input ), ._1___buffer_read(_3), .video(n32buffer_el_4_video), ._1___buffer_write___clr(show));
  _32buffer_el u_32buffer_el_5 (
    .\input (\input ), ._1___buffer_read(_4), .video(n32buffer_el_5_video), ._1___buffer_write___clr(show));
  _32buffer_el u_32buffer_el_6 (
    .\input (\input ), ._1___buffer_read(_5), .video(n32buffer_el_6_video), ._1___buffer_write___clr(show));
  _32buffer_el u_32buffer_el_7 (
    .\input (\input ), ._1___buffer_read(_6), .video(n32buffer_el_7_video), ._1___buffer_write___clr(show));
  _32buffer_el u_32buffer_el_8 (
    .\input (\input ), ._1___buffer_read(_7), .video(n32buffer_el_8_video), ._1___buffer_write___clr(show));
  _32buffer_el u_32buffer_el_9 (
    .\input (\input ), ._1___buffer_read(_8), .video(n32buffer_el_9_video), ._1___buffer_write___clr(show));
  _32buffer_el u_32buffer_el_10 (
    .\input (\input ), ._1___buffer_read(_9), .video(n32buffer_el_10_video), ._1___buffer_write___clr(show));
  _32buffer_el u_32buffer_el_11 (
    .\input (\input ), ._1___buffer_read(_10), .video(n32buffer_el_11_video), ._1___buffer_write___clr(show));
  _32buffer_el u_32buffer_el_12 (
    .\input (\input ), ._1___buffer_read(_11), .video(n32buffer_el_12_video), ._1___buffer_write___clr(show));
  _32buffer_el u_32buffer_el_13 (
    .\input (\input ), ._1___buffer_read(_12), .video(n32buffer_el_13_video), ._1___buffer_write___clr(show));
  _32buffer_el u_32buffer_el_14 (
    .\input (\input ), ._1___buffer_read(_13), .video(n32buffer_el_14_video), ._1___buffer_write___clr(show));
  _32buffer_el u_32buffer_el_15 (
    .\input (\input ), ._1___buffer_read(_14), .video(n32buffer_el_15_video), ._1___buffer_write___clr(show));
  _32buffer_el u_32buffer_el_16 (
    .\input (\input ), ._1___buffer_read(_15), .video(n32buffer_el_16_video), ._1___buffer_write___clr(show));
  _32buffer_el u_32buffer_el_17 (
    .\input (\input ), ._1___buffer_read(_16), .video(n32buffer_el_17_video), ._1___buffer_write___clr(show));
  _32buffer_el u_32buffer_el_18 (
    .\input (\input ), ._1___buffer_read(_17), .video(n32buffer_el_18_video), ._1___buffer_write___clr(show));
  _32buffer_el u_32buffer_el_19 (
    .\input (\input ), ._1___buffer_read(_18), .video(n32buffer_el_19_video), ._1___buffer_write___clr(show));
  _32buffer_el u_32buffer_el_20 (
    .\input (\input ), ._1___buffer_read(_19), .video(n32buffer_el_20_video), ._1___buffer_write___clr(show));
  _32buffer_el u_32buffer_el_21 (
    .\input (\input ), ._1___buffer_read(_20), .video(n32buffer_el_21_video), ._1___buffer_write___clr(show));
  _32buffer_el u_32buffer_el_22 (
    .\input (\input ), ._1___buffer_read(_21), .video(n32buffer_el_22_video), ._1___buffer_write___clr(show));
  _32buffer_el u_32buffer_el_23 (
    .\input (\input ), ._1___buffer_read(_22), .video(n32buffer_el_23_video), ._1___buffer_write___clr(show));
  _32buffer_el u_32buffer_el_24 (
    .\input (\input ), ._1___buffer_read(_23), .video(n32buffer_el_24_video), ._1___buffer_write___clr(show));
  _32buffer_el u_32buffer_el_25 (
    .\input (\input ), ._1___buffer_read(_24), .video(n32buffer_el_25_video), ._1___buffer_write___clr(show));
  _32buffer_el u_32buffer_el_26 (
    .\input (\input ), ._1___buffer_read(_25), .video(n32buffer_el_26_video), ._1___buffer_write___clr(show));
  _32buffer_el u_32buffer_el_27 (
    .\input (\input ), ._1___buffer_read(_26), .video(n32buffer_el_27_video), ._1___buffer_write___clr(show));
  _32buffer_el u_32buffer_el_28 (
    .\input (\input ), ._1___buffer_read(_27), .video(n32buffer_el_28_video), ._1___buffer_write___clr(show));
  _32buffer_el u_32buffer_el_29 (
    .\input (\input ), ._1___buffer_read(_28), .video(n32buffer_el_29_video), ._1___buffer_write___clr(show));
  _32buffer_el u_32buffer_el_30 (
    .\input (\input ), ._1___buffer_read(_29), .video(n32buffer_el_30_video), ._1___buffer_write___clr(show));
  _32buffer_el u_32buffer_el_31 (
    .\input (\input ), ._1___buffer_read(_30), .video(n32buffer_el_31_video), ._1___buffer_write___clr(show));
  _32buffer_el u_32buffer_el_32 (
    .\input (\input ), ._1___buffer_read(_31), .video(n32buffer_el_32_video), ._1___buffer_write___clr(show));
  assign out_37 = in_1 | n32buffer_el_1_video;  // OR_Gate or_1, 32 bits wide
  assign out_38 = in_2 | n32buffer_el_2_video;  // OR_Gate or_2, 32 bits wide
  assign out_39 = in_3 | n32buffer_el_3_video;  // OR_Gate or_3, 32 bits wide
  assign out_40 = in_4 | n32buffer_el_4_video;  // OR_Gate or_4, 32 bits wide
  assign out_41 = in_5 | n32buffer_el_5_video;  // OR_Gate or_5, 32 bits wide
  assign out_42 = in_6 | n32buffer_el_6_video;  // OR_Gate or_6, 32 bits wide
  assign out_43 = in_8 | n32buffer_el_7_video;  // OR_Gate or_7, 32 bits wide
  assign out_44 = in_12 | n32buffer_el_8_video;  // OR_Gate or_8, 32 bits wide
  assign out_45 = in_13 | n32buffer_el_9_video;  // OR_Gate or_9, 32 bits wide
  assign out_46 = in_14 | n32buffer_el_10_video;  // OR_Gate or_10, 32 bits wide
  assign out_47 = in_15 | n32buffer_el_11_video;  // OR_Gate or_11, 32 bits wide
  assign out_48 = in_16 | n32buffer_el_12_video;  // OR_Gate or_12, 32 bits wide
  assign out_49 = in_17 | n32buffer_el_13_video;  // OR_Gate or_13, 32 bits wide
  assign out_50 = in_18 | n32buffer_el_14_video;  // OR_Gate or_14, 32 bits wide
  assign out_51 = in_19 | n32buffer_el_15_video;  // OR_Gate or_15, 32 bits wide
  assign out_52 = in_20 | n32buffer_el_16_video;  // OR_Gate or_16, 32 bits wide
  assign out_53 = in_21 | n32buffer_el_17_video;  // OR_Gate or_17, 32 bits wide
  assign out_54 = in_22 | n32buffer_el_18_video;  // OR_Gate or_18, 32 bits wide
  assign out_55 = in_23 | n32buffer_el_19_video;  // OR_Gate or_19, 32 bits wide
  assign out_56 = in_24 | n32buffer_el_20_video;  // OR_Gate or_20, 32 bits wide
  assign out_57 = in_25 | n32buffer_el_21_video;  // OR_Gate or_21, 32 bits wide
  assign out_58 = in_26 | n32buffer_el_22_video;  // OR_Gate or_22, 32 bits wide
  assign out_59 = in_27 | n32buffer_el_23_video;  // OR_Gate or_23, 32 bits wide
  assign out_60 = in_28 | n32buffer_el_24_video;  // OR_Gate or_24, 32 bits wide
  assign out_61 = in_29 | n32buffer_el_25_video;  // OR_Gate or_25, 32 bits wide
  assign out_62 = in_30 | n32buffer_el_26_video;  // OR_Gate or_26, 32 bits wide
  assign out_63 = in_31 | n32buffer_el_27_video;  // OR_Gate or_27, 32 bits wide
  assign out_64 = in_32 | n32buffer_el_28_video;  // OR_Gate or_28, 32 bits wide
  assign out_65 = in_33 | n32buffer_el_29_video;  // OR_Gate or_29, 32 bits wide
  assign out_66 = in_34 | n32buffer_el_30_video;  // OR_Gate or_30, 32 bits wide
  assign out_67 = in_35 | n32buffer_el_31_video;  // OR_Gate or_31, 32 bits wide
  assign out_68 = in_36 | n32buffer_el_32_video;  // OR_Gate or_32, 32 bits wide

  // Other names for the same wires on the sheet: inp[31:0] = \input ; w = show

  // Notes on the sheet:
  //   in_21: pull=down
  //   in_28: pull=down
  //   in_29: pull=down
  //   in_24: pull=down
  //   in_31: pull=down
  //   in_12: pull=down
  //   in_27: pull=down
  //   in_17: pull=down
  //   in_5: pull=down
  //   in_6: pull=down
  //   in_19: pull=down
  //   in_1: pull=down
  //   in_33: pull=down
  //   in_30: pull=down
  //   in_35: pull=down
  //   in_23: pull=down
  //   in_36: pull=down
  //   in_3: pull=down
  //   in_15: pull=down
  //   in_22: pull=down
  //   write: pull=down
  //   in_18: pull=down
  //   in_20: pull=down
  //   in_4: pull=down
  //   in_25: pull=down
  //   in_34: pull=down
  //   in_26: pull=down
  //   in_32: pull=down
  //   in_8: pull=down
  //   in_13: pull=down
  //   in_2: pull=down
  //   in_16: pull=down
  //   in_14: pull=down
endmodule

module priority_thread_selector (
  input  request,
  input  request_2,
  input  request_3,
  output access,
  output access_2,
  output access_3,
  output writing
);

  wire blocker_1_out_3, blocker_2_out_3, request_wait_1_out, request_wait_2_out, request_wait_3_out;

  request_wait request_wait_1 (.\wait (writing), .write(request), .out(request_wait_1_out));
  blocker blocker_1 (.out_3(blocker_1_out_3), .in_1(request_wait_1_out), .out_4(access));  // open: in_2
  buf buffer_1 (writing, access);
  Pull_Resistor pull_resistor_1 (.node(writing));
  request_wait request_wait_2 (.\wait (writing), .write(request_2), .out(request_wait_2_out));
  blocker blocker_2 (.out_3(blocker_2_out_3), .in_1(request_wait_2_out), .out_4(access_2), .in_2(blocker_1_out_3));
  buf buffer_2 (writing, access_2);
  request_wait request_wait_3 (.\wait (writing), .write(request_3), .out(request_wait_3_out));
  blocker blocker_3 (.in_1(request_wait_3_out), .out_4(access_3), .in_2(blocker_2_out_3));  // open: out_3
  buf buffer_3 (writing, access_3);

  // Notes on the sheet:
  //   buffer_1 drives only 1 and floats otherwise
  //   buffer_2 drives only 1 and floats otherwise
  //   buffer_3 drives only 1 and floats otherwise
endmodule

module request_wait (
  input  \wait ,
  input  write,
  output out
);

  wire or_1_out;

  or or_1 (or_1_out, out, ~\wait );  // OR_Gate
  D_Flip_Flop #(.trigger("high")) d_ff_1 (.clk(or_1_out), .D(write), .Q(out));  // open: Qn, preset, en, reset
endmodule

module blocker (
  input  in_1,
  input  in_2,
  output out_3,
  output out_4
);

  and and_1 (out_4, ~in_2, in_1);  // AND_Gate
  or or_1 (out_3, in_2, out_4);

  // Notes on the sheet:
  //   in_2: pull=down
endmodule

module drawer (
  input  [15:0] in_1,
  input  [4:0] in_2,
  input  [4:0] in_3,
  input  [15:0] in_4,
  input  clk,
  output out_6,
  output out_7,
  output [31:0] out_8,
  output [4:0] out_9,
  output out_10
);

  wire activator_q, and_1_out, counter_1_carry, drawing, not_1_out, pull_resistor_1_node, transistor_1_out;
  wire [4:0] counter_1_q;
  wire [15:0] adder_1_out, bit_extender_1_out, multiplier_1_out;
  wire [31:0] rom_1_data;

  simple_drawer_32x32 simple_drawer_32x32_1 (
    .x(in_2), .y(in_3), .texture_line(counter_1_q), .texture_input(rom_1_data), .cur_line(out_9),
    .line_x1(out_8));
  Counter #(.width(5), .max('h2)) counter_1 (
    .Q(counter_1_q), .carry(counter_1_carry), .clk(transistor_1_out), .clr(and_1_out));  // open: load, D, count
  Transistor #(.\type ("n"), .gate("br")) transistor_1 (.in(clk), .out(transistor_1_out), .gate(drawing));
  and and_1 (and_1_out, ~clk, counter_1_carry);  // AND_Gate
  D_Flip_Flop #(.trigger("falling")) synchronizer (
    .clk(clk), .D(activator_q), .Q(drawing), .reset(and_1_out));  // open: Qn, preset, en
  D_Flip_Flop activator (
    .clk(pull_resistor_1_node), .D(pull_resistor_1_node), .Q(activator_q), .reset(and_1_out));  // open: Qn, preset, en
  or or_1 (out_6, drawing, activator_q, and_1_out);
  assign bit_extender_1_out = {{11{1'b0}}, counter_1_q};  // Bit_Extender bit_extender_1
  Multiplier #(.width(16)) multiplier_1 (.a(in_1), .b(16'h3), .out(multiplier_1_out));  // open: cin, cout
  // Probe on in_1
  Adder #(.width(16)) adder_1 (.a(bit_extender_1_out), .b(multiplier_1_out), .out(adder_1_out));  // open: cin, cout
  Pull_Resistor pull_resistor_1 (.node(pull_resistor_1_node));
  Comparator #(.width(16), .mode("unsigned")) comparator_1 (
    .a(in_4), .b(16'h1), .eq(pull_resistor_1_node));  // open: gt, lt
  Comparator #(.width(16), .mode("unsigned")) comparator_2 (.a(in_4), .b(16'h2), .eq(out_10));  // open: gt, lt
  Pull_Resistor pull_resistor_2 (.node(out_10));
  and and_2 (out_7, drawing, not_1_out);
  not not_1 (not_1_out, clk);
  ROM #(.addrWidth(16), .dataWidth(32)) rom_1 (.addr(adder_1_out), .data(rom_1_data));  // open: sel

  // Other names for the same wires on the sheet: cmd_show = out_10

  // Notes on the sheet:
  //   texture line counter
  //   contents of rom_1 (hex, n*v repeats v):
  //   2 7 5 2 5 5 0 0 0 2 7 5 2 5 5 7 5 5 2 7 7 2 5 7 2 5 5 0 0 0 1 1 1 1151 1351 1551 1955 1155 114a
  //   7ce381 41441 3ce441 50441 51441 7ce39f 1 1 1 0 0 0 2 1 0 2 3 0 3 3
endmodule

module requester (
  input  make_request,
  input  response,
  input  writing_data,
  output permission_received,
  output request
);

  wire and_1_out, and_2_out, d_ff_1_q, d_ff_1_qn, or_1_out, register_1_q;

  D_Flip_Flop d_ff_1 (
    .clk(make_request), .D(make_request), .Q(d_ff_1_q), .Qn(d_ff_1_qn), .reset(writing_data));  // open: preset, en
  Register #(.width(1)) register_1 (.D(d_ff_1_q), .Q(register_1_q), .clk(writing_data), .clr(and_1_out));  // open: en
  and and_1 (and_1_out, d_ff_1_qn, ~writing_data);  // AND_Gate
  or or_1 (or_1_out, d_ff_1_q, and_2_out);
  and and_2 (and_2_out, register_1_q, writing_data);
  buf buffer_1 (request, or_1_out);
  and and_3 (permission_received, or_1_out, response);

  // Notes on the sheet:
  //   response: pull=down
  //   writing_data: pull=down
  //   make_request: pull=down
  //   buffer_1 drives only 1 and floats otherwise
endmodule

module bullet_thread (
  input  run,
  input  drawing,
  input  [15:0] adr,
  input  clk,
  input  [15:0] val,
  input  write,
  input  collided,
  input  end_cycle,
  output [15:0] id,
  output [4:0] x,
  output [4:0] y,
  output [15:0] command,
  output collide_check_player,
  output collide_check_enemy,
  output collide_check_wall,
  output [15:0] x_col,
  output [15:0] y_col
);

  wire and_1_out, and_2_out, and_6_out, and_7_out, and_8_out, and_9_out, and_10_out, and_11_out, and_12_out,
       and_13_out, bot, bullet_object_1_avaiable, bullet_object_1_ready, bullet_object_2_avaiable,
       bullet_object_2_ready, bullet_object_3_avaiable, bullet_object_3_ready, bullet_object_4_avaiable,
       bullet_object_4_ready, command_draw, comparator_1_eq, comparator_2_eq, comparator_6_eq,
       comparator_9_eq, counter_1_carry, cycle, d_ff_1_qn, d_ff_2_qn, enemy, enemy1, enemy2, or_1_out,
       or_2_out, player, pull_resistor_4_node, pull_resistor_5_node, pull_resistor_6_node,
       pull_resistor_9_node, runnable, xor_1_out;
  wire [15:0] bullet_object_1_x, bullet_object_1_y, button_q, divider_1_out, divider_2_out, enemy_spawn_x,
       enemy_spawn_y, player_spawn_x, player_spawn_y, rand_q, shifter_1_out, shifter_2_out, spawn_x, spawn_y;

  and and_1 (and_1_out, run, runnable);
  D_Flip_Flop d_ff_1 (.clk(cycle), .D(cycle), .Qn(d_ff_1_qn), .reset(counter_1_carry));  // open: Q, preset, en
  or or_1 (or_1_out, bot, player, enemy);
  Counter #(.width(2), .max('h3)) counter_1 (
    .carry(counter_1_carry), .clk(clk), .clr(d_ff_1_qn));  // open: load, D, count, Q
  and and_2 (and_2_out, runnable, or_1_out);
  xor xor_1 (xor_1_out, counter_1_carry, and_1_out);
  bullet_object bullet_object_1 (
    .draw(xor_1_out), .spawn_id(16'hf), .spawn_x(enemy_spawn_x), .spawn_y(enemy_spawn_y), .y_vec(16'h2),
    .ready(bullet_object_1_ready), .id(id), .x(bullet_object_1_x), .y(bullet_object_1_y), .command(command),
    .avaiable(bullet_object_1_avaiable), .clk(clk), .end_cycle(end_cycle), .delete(collided), .spawn(enemy1),
    .\wait (drawing));
  and and_3 (enemy1, bullet_object_1_avaiable, enemy);
  bullet_object bullet_object_2 (
    .draw(bullet_object_1_ready), .spawn_id(16'hf), .spawn_x(enemy_spawn_x), .spawn_y(enemy_spawn_y),
    .y_vec(16'h2), .ready(bullet_object_2_ready), .id(id), .x(bullet_object_1_x), .y(bullet_object_1_y),
    .command(command), .avaiable(bullet_object_2_avaiable), .clk(clk), .end_cycle(end_cycle),
    .delete(collided), .spawn(enemy2), .\wait (drawing));
  and and_4 (runnable, bullet_object_1_avaiable, bullet_object_2_avaiable, bullet_object_3_avaiable, bullet_object_4_avaiable);
  and and_5 (enemy2, ~bullet_object_1_avaiable, bullet_object_2_avaiable, enemy);  // AND_Gate
  bullet_object bullet_object_3 (
    .draw(bullet_object_2_ready), .spawn_id(16'ha), .spawn_x(player_spawn_x), .spawn_y(player_spawn_y),
    .y_vec(16'hfffe), .ready(bullet_object_3_ready), .id(id), .x(bullet_object_1_x), .y(bullet_object_1_y),
    .command(command), .avaiable(bullet_object_3_avaiable), .clk(clk), .end_cycle(end_cycle),
    .delete(collided), .spawn(player), .\wait (drawing));
  Pull_Resistor pull_resistor_1 (.node(bot));
  bullet_object bullet_object_4 (
    .draw(bullet_object_3_ready), .spawn_id(16'ha), .spawn_x(spawn_x), .spawn_y(spawn_y), .y_vec(16'hfffe),
    .ready(bullet_object_4_ready), .id(id), .x(bullet_object_1_x), .y(bullet_object_1_y), .command(command),
    .avaiable(bullet_object_4_avaiable), .clk(clk), .end_cycle(end_cycle), .delete(collided), .spawn(bot),
    .\wait (drawing));
  Counter #(.width(2), .max('h3)) counter_2 (.carry(cycle), .clk(clk), .clr(d_ff_2_qn));  // open: load, D, count, Q
  D_Flip_Flop d_ff_2 (
    .clk(bullet_object_4_ready), .D(bullet_object_4_ready), .Qn(d_ff_2_qn), .reset(cycle));  // open: Q, preset, en
  and and_6 (and_6_out, comparator_1_eq, clk, write);
  Comparator #(.width(16), .mode("unsigned")) comparator_1 (.a(adr), .b(16'h80), .eq(comparator_1_eq));  // open: gt, lt
  Pull_Resistor pull_resistor_2 (.node(comparator_1_eq));
  and and_7 (and_7_out, comparator_2_eq, clk, write);
  Comparator #(.width(16), .mode("unsigned")) comparator_2 (.a(adr), .b(16'h82), .eq(comparator_2_eq));  // open: gt, lt
  Pull_Resistor pull_resistor_3 (.node(comparator_2_eq));
  and and_8 (and_8_out, pull_resistor_4_node, clk, write);
  Pull_Resistor pull_resistor_4 (.node(pull_resistor_4_node));
  Comparator #(.width(16), .mode("unsigned")) comparator_3 (
    .a(adr), .b(16'hac), .eq(pull_resistor_4_node));  // open: gt, lt
  and and_9 (and_9_out, pull_resistor_5_node, clk, write);
  Pull_Resistor pull_resistor_5 (.node(pull_resistor_5_node));
  Comparator #(.width(16), .mode("unsigned")) comparator_4 (
    .a(adr), .b(16'ha8), .eq(pull_resistor_5_node));  // open: gt, lt
  and and_10 (and_10_out, pull_resistor_6_node, clk, write);
  Pull_Resistor pull_resistor_6 (.node(pull_resistor_6_node));
  Comparator #(.width(16), .mode("unsigned")) comparator_5 (
    .a(adr), .b(16'haa), .eq(pull_resistor_6_node));  // open: gt, lt
  and and_11 (and_11_out, comparator_6_eq, clk, write);
  Comparator #(.width(16), .mode("unsigned")) comparator_6 (.a(adr), .b(16'ha0), .eq(comparator_6_eq));  // open: gt, lt
  Pull_Resistor pull_resistor_7 (.node(comparator_6_eq));
  Transistor #(.width(16)) transistor_1 (.in(16'h2), .out(command), .gate(d_ff_2_qn));
  Register #(.width(16)) enemy_x (.D(val), .Q(enemy_spawn_x), .clk(and_6_out));  // open: en, clr
  Register #(.width(16)) enemy_y (.D(val), .Q(enemy_spawn_y), .clk(and_7_out));  // open: en, clr
  Register #(.width(16)) \rand  (.D(val), .Q(rand_q), .clk(and_8_out), .clr(enemy));  // open: en
  Register #(.width(16)) player_x (.D(val), .Q(player_spawn_x), .clk(and_9_out));  // open: en, clr
  Register #(.width(16)) player_y (.D(val), .Q(player_spawn_y), .clk(and_10_out));  // open: en, clr
  Register #(.width(16)) button (.D(val), .Q(button_q), .clk(and_11_out), .clr(player));  // open: en
  Divider #(.width(16)) divider_1 (.a(bullet_object_1_x), .b(16'h2), .out(divider_1_out));  // open: upper, rem
  Comparator #(.width(16), .mode("unsigned")) comparator_7 (.a(rand_q), .b(16'h3), .eq(enemy));  // open: gt, lt
  Comparator #(.width(16), .mode("unsigned")) comparator_8 (.a(button_q), .b(16'h1), .eq(player));  // open: gt, lt
  Shifter #(.width(16), .shift("lr")) shifter_1 (.in(bullet_object_1_x), .\dist (4'b0001), .out(shifter_1_out));
  Bit_Extender #(.in_width(16), .out_width(5)) bit_extender_1 (.in(shifter_1_out), .out(x));
  Register #(.width(16)) u_x (.D(divider_1_out), .Q(x_col), .clk(or_2_out));  // open: en, clr
  Shifter #(.width(16), .shift("lr")) shifter_2 (.in(bullet_object_1_y), .\dist (4'b0001), .out(shifter_2_out));
  Register #(.width(16)) u_y (.D(divider_2_out), .Q(y_col), .clk(or_2_out));  // open: en, clr
  Divider #(.width(16)) divider_2 (.a(bullet_object_1_y), .b(16'h2), .out(divider_2_out));  // open: upper, rem
  Bit_Extender #(.in_width(16), .out_width(5)) bit_extender_2 (.in(shifter_2_out), .out(y));
  Comparator #(.width(16), .mode("unsigned")) comparator_9 (.a(id), .b(16'hf), .eq(comparator_9_eq));  // open: gt, lt
  Pull_Resistor pull_resistor_8 (.node(comparator_9_eq));
  Pull_Resistor pull_resistor_9 (.node(pull_resistor_9_node));
  Comparator #(.width(16), .mode("unsigned")) comparator_10 (
    .a(id), .b(16'ha), .eq(pull_resistor_9_node));  // open: gt, lt
  Pull_Resistor pull_resistor_10 (.node(command_draw));
  Comparator #(.width(16), .mode("unsigned")) comparator_11 (
    .a(command), .b(16'h1), .eq(command_draw));  // open: gt, lt
  and and_12 (and_12_out, command_draw, comparator_9_eq);
  and and_13 (and_13_out, command_draw, pull_resistor_9_node);
  or or_2 (or_2_out, and_13_out, and_12_out);
  D_Flip_Flop d_ff_3 (.clk(clk), .D(and_12_out), .Q(collide_check_player));  // open: Qn, preset, en, reset
  D_Flip_Flop d_ff_4 (.clk(clk), .D(and_13_out), .Q(collide_check_enemy));  // open: Qn, preset, en, reset
  D_Flip_Flop d_ff_5 (.clk(clk), .D(or_2_out), .Q(collide_check_wall));  // open: Qn, preset, en, reset

  // Other names for the same wires on the sheet: wait = drawing

  // Notes on the sheet:
  //   collided: pull=down
  //   Enemy bullets
  //   Allied bullets
endmodule

module bullet_object (
  input  end_cycle,
  input  draw,
  input  [15:0] spawn_id,
  input  [15:0] spawn_x,
  input  [15:0] spawn_y,
  input  delete,
  input  [15:0] y_vec,
  input  spawn,
  input  clk,
  input  \wait ,
  output avaiable,
  output ready,
  output [15:0] id,
  output [15:0] x,
  output [15:0] y,
  output [15:0] command
);

  wire activator_q, and_2_out, and_3_out, and_4_out, comparator_2_gt, comparator_3_lt, counter_1_carry,
       delete_t, draw_t, \end , or_1_out, pull_resistor_2_node, skip, update;
  wire [1:0] counter_1_q;
  wire [15:0] adder_1_out, adder_2_out, bit_extender_1_out, id_q, multiplexer_1_out, multiplexer_2_out,
       multiplexer_3_out, x_q, y_q;

  and and_1 (skip, avaiable, draw);
  D_Flip_Flop activator (.clk(draw), .D(draw), .Q(activator_q), .reset(or_1_out));  // open: Qn, preset, en
  Pull_Resistor pull_resistor_1 (.node(spawn_id));
  D_Flip_Flop #(.trigger("falling")) synchronizer (
    .clk(clk), .D(activator_q), .Q(draw_t), .reset(or_1_out));  // open: Qn, preset, en
  or or_1 (or_1_out, end_cycle, ready);
  Adder #(.width(16)) adder_1 (.a(y_q), .b(y_vec), .out(adder_1_out));  // open: cin, cout
  Multiplexer #(.width(16), .enable("false")) multiplexer_1 (
    .in0(id_q), .in1(spawn_id), .out(multiplexer_1_out), .sel(avaiable));
  Multiplexer #(.width(16), .enable("false")) multiplexer_2 (
    .in0(x_q), .in1(spawn_x), .out(multiplexer_2_out), .sel(avaiable));
  Multiplexer #(.width(16), .enable("false")) multiplexer_3 (
    .in0(adder_1_out), .in1(spawn_y), .out(multiplexer_3_out), .sel(avaiable));
  Counter #(.width(2), .max('h2)) counter_1 (
    .Q(counter_1_q), .carry(counter_1_carry), .clk(pull_resistor_2_node), .clr(counter_1_carry));  // open: load, D, count
  Pull_Resistor pull_resistor_2 (.node(pull_resistor_2_node));
  assign pull_resistor_2_node = and_2_out ? clk : 1'bz;  // Controlled_Buffer controlled_buffer_1
  and and_2 (and_2_out, draw_t, ~\wait );  // AND_Gate
  Comparator #(.width(16), .mode("unsigned")) comparator_1 (.a({16{1'b0}}), .b(id_q), .eq(avaiable));  // open: gt, lt
  Register #(.width(16)) u_id (.D(multiplexer_1_out), .Q(id_q), .clk(update), .clr(delete_t));  // open: en
  Register #(.width(16)) u_x (.D(multiplexer_2_out), .Q(x_q), .clk(update), .clr(delete_t));  // open: en
  Register #(.width(16)) u_y (.D(multiplexer_3_out), .Q(y_q), .clk(update), .clr(delete_t));  // open: en
  assign bit_extender_1_out = {{15{1'b0}}, counter_1_q[0]};  // Bit_Extender bit_extender_1
  timer timer_1 (.run(counter_1_carry), .out(\end ), .clk_2(clk), .clk(16'h4));
  assign id = draw_t ? id_q : 16'bz;  // Controlled_Buffer controlled_buffer_2
  Adder #(.width(16)) adder_2 (.a(x_q), .b(16'h2), .out(adder_2_out));  // open: cin, cout
  assign y = draw_t ? y_q : 16'bz;  // Controlled_Buffer controlled_buffer_3
  assign command = draw_t ? bit_extender_1_out : 16'bz;  // Controlled_Buffer controlled_buffer_4
  assign x = draw_t ? adder_2_out : 16'bz;  // Controlled_Buffer controlled_buffer_5
  and and_3 (and_3_out, avaiable, draw_t);
  or or_2 (update, spawn, draw_t);
  or or_3 (ready, \end , and_3_out, skip, delete_t);
  Comparator #(.width(16), .mode("unsigned")) comparator_2 (.a(y_q), .b(16'h3b), .gt(comparator_2_gt));  // open: eq, lt
  Comparator #(.width(16), .mode("unsigned")) comparator_3 (
    .a(y_q), .b({16{1'b0}}), .lt(comparator_3_lt));  // open: gt, eq
  and and_4 (and_4_out, delete, draw_t);
  or or_4 (delete_t, comparator_2_gt, comparator_3_lt, and_4_out);

  // Notes on the sheet:
  //   spawn: pull=down
  //   end_cycle: pull=down
endmodule

module timer (
  input  run,
  input  [15:0] clk,
  input  clk_2,
  output out
);

  wire d_ff_1_qn;
  wire [15:0] counter_1_q;

  D_Flip_Flop d_ff_1 (.clk(run), .D(run), .Qn(d_ff_1_qn), .reset(out));  // open: Q, preset, en
  Counter #(.width(16), .max('hffff)) counter_1 (
    .Q(counter_1_q), .clk(clk_2), .clr(d_ff_1_qn));  // open: load, D, count, carry
  Comparator #(.width(16), .mode("unsigned")) comparator_1 (.a(counter_1_q), .b(clk), .eq(out));  // open: gt, lt

  // Other names for the same wires on the sheet: clk_t = clk_2
endmodule
